// Logisim project shematic.circ as structural Verilog: 22 circuits, main circuit main
module main (
  input  clk,
  input  rst,
  input  [31:0] Jin,
  input  Jen,
  output InstDone,
  output [8:0] ch,
  output [31:0] R1,
  output [31:0] R2,
  output [31:0] R3,
  output [31:0] R4,
  output [31:0] R5,
  output [31:0] R6,
  output [31:0] R7,
  output [31:0] IRR,
  output [31:0] R8,
  output [31:0] R9,
  output [31:0] R10,
  output [31:0] R11,
  output [31:0] R12,
  output [31:0] R13,
  output [31:0] R14,
  output [31:0] R15,
  output [31:0] R16,
  output [3:0] aluop,
  output [31:0] R17,
  output [31:0] R18,
  output [31:0] R19,
  output [31:0] R20,
  output [31:0] R21,
  output [31:0] R22,
  output [31:0] R23,
  output [31:0] R24,
  output [31:0] R25,
  output [31:0] R26,
  output [31:0] R27,
  output [31:0] R28,
  output [31:0] R29,
  output [31:0] R30,
  output [31:0] R31,
  output [31:0] Jout
);

  wire ALU_unit_done, ALUSrc, and_1_out, and_2_out, and_3_out, and_4_out, and_5_out, BranchEQ, BranchNEQ,
       comparator_1_gt, comparator_2_eq, comparator_3_eq, div, div_mult_done, done, exe, hi, InstructionD,
       InstructionF, jal, jr, Jump, mem, mem_to_reg, MemWrite, mf, mul, nand_1_out, not_1_out, not_2_out,
       not_3_out, not_4_out, or_1_out, or_2_out, or_3_out, or_4_out, RegDst, register_1_q, RegWrite, sll_s,
       slti, wb;
  wire [4:0] destination, multiplexer_3_out, multiplexer_4_out;
  wire [8:0] adder_1_out, adder_2_out, adder_3_out, jalpc, multiplexer_12_out, multiplexer_14_out,
       multiplexer_15_out, pc;
  wire [31:0] A, a_t, alu_out, alu_out2, alu_out_hi, aluin1, b, B_q, bit_extender_1_out, bit_extender_2_out,
       bit_extender_3_out, D_MEM_dout, Dwrite, I_MEM_dout, J_out, MDR_q, mfhi, mflo, mfout,
       multiplexer_2_out, multiplexer_5_out, multiplexer_6_out, multiplexer_8_out, multiplexer_10_out,
       multiplexer_11_out, multiplexer_18_out, multiplexer_19_out, reg2;
  wire [63:0] shifter_shifted;

  Register #(.width(32)) IR (.D(I_MEM_dout), .en(InstructionF), .clk(clk), .Q(IRR));  // open: clr
  Register #(.width(32)) lo (.D(alu_out), .en(div), .clk(clk), .Q(mflo));  // open: clr
  Register #(.width(32)) u_hi (.D(alu_out_hi), .en(div), .clk(clk), .Q(mfhi));  // open: clr
  Register #(.width(9)) u_PC (.D(pc), .clk(clk), .Q(ch), .clr(rst));  // open: en
  and and_1 (and_1_out, done, MemWrite);
  CONTROL all_control (
    .opcode(IRR[31:26]), .func(IRR[5:0]), .exe(exe), .aluOp(aluop), .mem_to_reg(mem_to_reg), .RegDst(RegDst),
    .MemWrite(MemWrite), .RegWrite(RegWrite), .Div(div), .BranchNEQ(BranchNEQ), .Jump(Jump), .ALUSrc(ALUSrc),
    .sll_s(sll_s), .slti(slti), .mf(mf), .hi(hi), .mul(mul), .BranchEQ(BranchEQ), .jr(jr), .jal(jal));
  LSR shifter (.a(alu_out), .b(32'h2), .shifted(shifter_shifted));
  D_Flip_Flop d_ff_1 (.D(wb), .clk(clk), .Q(InstDone));  // open: Qn, preset, reset
  Comparator #(.width(32)) comparator_1 (.a({32{1'b0}}), .b(Dwrite), .gt(comparator_1_gt));  // open: eq, lt
  assign bit_extender_1_out = {{31{1'b0}}, comparator_1_gt};  // Bit_Extender bit_extender_1
  and and_2 (and_2_out, RegWrite, wb);
  jtag_ram512 D_MEM (
    .clk(clk), .Jen(Jen), .Din(reg2), .Jin(J_out), .Wen(and_1_out), .Addr(shifter_shifted[8:0]), .Jout(Jout),
    .Dout(D_MEM_dout));
  Multiplexer #(.width(32)) multiplexer_1 (.in0(mflo), .in1(mfhi), .out(mfout), .sel(hi));
  Multiplexer #(.width(32)) multiplexer_2 (.in0(Dwrite), .in1(bit_extender_1_out), .out(multiplexer_2_out), .sel(slti));
  Multiplexer #(.width(5)) multiplexer_3 (.in0({5{1'b0}}), .in1(destination), .out(multiplexer_3_out), .sel(and_2_out));
  Register #(.width(32)) MDR (.D(D_MEM_dout), .en(mem), .clk(clk), .Q(MDR_q));  // open: clr
  jtag_ram512 I_MEM (.clk(clk), .Jen(Jen), .Jin(Jin), .Addr(ch), .Jout(J_out), .Dout(I_MEM_dout));  // open: Din, Wen
  Multiplexer #(.width(5)) multiplexer_4 (.in0(multiplexer_3_out), .in1({5{1'b1}}), .out(multiplexer_4_out), .sel(jal));
  Register #(.width(32)) u_B (.D(reg2), .clk(clk), .Q(B_q));  // open: en, clr
  Multiplexer #(.width(32)) multiplexer_5 (.in0(alu_out), .in1(MDR_q), .out(multiplexer_5_out), .sel(mem_to_reg));
  Adder #(.width(9)) adder_1 (.a(ch), .b(9'h1), .out(adder_1_out));  // open: cin, cout
  Register #(.width(9)) pc_jal (.D(adder_1_out), .en(InstructionF), .clk(clk), .Q(jalpc));  // open: clr
  regfile Reg_File (
    .clk(clk), .rst(rst), .Dwrite(multiplexer_2_out), .Awrite(multiplexer_4_out), .Aread0(IRR[25:21]),
    .Aread1(IRR[20:16]), .Dread0(a_t), .Dread1(reg2), .R1(R1), .R2(R2), .R3(R3), .R4(R4), .R5(R5), .R6(R6),
    .R7(R7), .R8(R8), .R9(R9), .R10(R10), .R11(R11), .R12(R12), .R13(R13), .R14(R14), .R15(R15), .R16(R16),
    .R17(R17), .R18(R18), .R19(R19), .R20(R20), .R21(R21), .R22(R22), .R23(R23), .R24(R24), .R25(R25),
    .R26(R26), .R27(R27), .R28(R28), .R29(R29), .R30(R30), .R31(R31));
  Multiplexer #(.width(32)) multiplexer_6 (.in0(multiplexer_5_out), .in1(mfout), .out(multiplexer_6_out), .sel(mf));
  assign bit_extender_2_out = {{16{IRR[15]}}, IRR[15:0]};  // Bit_Extender bit_extender_2
  Multiplexer #(.width(32)) multiplexer_7 (.in0(multiplexer_6_out), .in1({{23{1'b0}}, jalpc}), .out(Dwrite), .sel(jal));
  Multiplexer #(.width(32)) multiplexer_8 (.in0(B_q), .in1(bit_extender_2_out), .out(multiplexer_8_out), .sel(ALUSrc));
  Multiplexer #(.width(5)) multiplexer_9 (.in0(IRR[15:11]), .in1(IRR[20:16]), .out(destination), .sel(RegDst));
  assign bit_extender_3_out = {{27{IRR[10]}}, IRR[10:6]};  // Bit_Extender bit_extender_3
  not not_1 (not_1_out, comparator_2_eq);
  Comparator #(.width(32)) comparator_2 (.a({32{1'b0}}), .b(alu_out2), .eq(comparator_2_eq));  // open: gt, lt
  Comparator #(.width(32)) comparator_3 (.a({32{1'b0}}), .b(alu_out2), .eq(comparator_3_eq));  // open: gt, lt
  and and_3 (and_3_out, BranchNEQ, not_1_out);
  and and_4 (and_4_out, BranchEQ, comparator_3_eq);
  Multiplexer #(.width(32)) multiplexer_10 (
    .in0(multiplexer_8_out), .in1(bit_extender_3_out), .out(multiplexer_10_out), .sel(sll_s));
  Multiplexer #(.width(32)) multiplexer_11 (
    .in0(multiplexer_10_out), .in1(32'h1), .out(multiplexer_11_out), .sel(InstructionF));
  ALU ALU_unit (
    .a(aluin1), .b(b), .aluop(aluop), .clk(clk), .rst(rst), .res_low(alu_out2), .done(ALU_unit_done),
    .res_high(alu_out_hi));  // open: output_inverted, output_inc
  Multiplexer #(.width(9)) multiplexer_12 (.in0(ch), .in1(alu_out[8:0]), .out(multiplexer_12_out), .sel(or_1_out));
  or or_1 (or_1_out, and_3_out, and_4_out);
  Multiplexer #(.width(32)) multiplexer_13 (
    .in0(multiplexer_11_out), .in1(bit_extender_2_out), .out(b), .sel(InstructionD));
  and and_5 (and_5_out, exe, not_2_out);
  not not_2 (not_2_out, done);
  Multiplexer #(.width(9)) multiplexer_14 (
    .in0(multiplexer_12_out), .in1(IRR[8:0]), .out(multiplexer_14_out), .sel(or_2_out));
  or or_2 (or_2_out, Jump, jal);
  Register #(.width(1)) register_1 (.D(ALU_unit_done), .clk(clk), .Q(register_1_q));  // open: en, clr
  Multiplexer #(.width(9)) multiplexer_15 (.in0(multiplexer_14_out), .in1(A[8:0]), .out(multiplexer_15_out), .sel(jr));
  Register #(.width(32)) u_A (.D(a_t), .clk(clk), .Q(A));  // open: en, clr
  not not_3 (not_3_out, register_1_q);
  Adder #(.width(9)) adder_2 (.a(ch), .b(9'h1), .out(adder_2_out));  // open: cin, cout
  Adder #(.width(9)) adder_3 (.a(ch), .b(9'h1), .out(adder_3_out));  // open: cin, cout
  Multiplexer multiplexer_16 (.in0(ALU_unit_done), .in1(div_mult_done), .out(done), .sel(or_3_out));
  or or_3 (or_3_out, div, mul);
  and and_6 (div_mult_done, not_3_out, ALU_unit_done);
  Multiplexer #(.width(9)) multiplexer_17 (.in0(multiplexer_15_out), .in1(adder_2_out), .out(pc), .sel(InstructionF));
  State_Finder stateFinder (
    .halt(and_5_out), .clk(clk), .reset(rst), .instruction_fetch(InstructionF),
    .instruction_decode(InstructionD), .exec(exe), .mem(mem), .wb(wb));
  Multiplexer #(.width(32)) multiplexer_18 (
    .in0(alu_out2), .in1({{23{1'b0}}, adder_3_out}), .out(multiplexer_18_out), .sel(jal));
  not not_4 (not_4_out, exe);
  Multiplexer #(.width(32)) multiplexer_19 (.in0(A), .in1(reg2), .out(multiplexer_19_out), .sel(sll_s));
  nand nand_1 (nand_1_out, jal, not_4_out);
  Multiplexer #(.width(32)) multiplexer_20 (
    .in0(multiplexer_19_out), .in1({{23{1'b0}}, ch}), .out(aluin1), .sel(or_4_out));
  or or_4 (or_4_out, InstructionF, InstructionD);
  Register #(.width(32)) ALUOut (.D(multiplexer_18_out), .en(nand_1_out), .clk(clk), .Q(alu_out));  // open: clr

  // Other names for the same wires on the sheet: func[5:0] = IRR[5:0]; immediate[15:0] = IRR[15:0];
  //   shamt[4:0] = IRR[10:6]; rd[4:0] = IRR[15:11]; rt[4:0] = IRR[20:16]; rs[4:0] = IRR[25:21]; Op[5:0] = IRR[31:26]
endmodule

module ALU (
  input  [31:0] a,
  input  [31:0] b,
  input  [3:0] aluop,
  input  output_inverted,
  input  output_inc,
  input  clk,
  input  rst,
  output [31:0] res_low,
  output done,
  output [31:0] res_high
);

  wire adder_2_cout, comparator_1_eq, comparator_2_eq, comparator_3_eq, comparator_4_eq, comparator_5_eq,
       done_DIV, done_MULT, not_2_out, not_3_out, not_4_out, or_1_out, or_2_out, start, SUB_cout;
  wire [0:0] ADD_HIGH;
  wire [3:0] aluop_Reg_q;
  wire [31:0] a_Reg_q, ADD_LOW, adder_1_out, adder_2_out, AND_LOW, ASR_HIGH, ASR_LOW, b_Reg_q, CLO_HIGH,
       CLO_LOW, CLZ_HIGH, CLZ_LOW, DIV_HIGH, DIV_LOW, LSL_HIGH, LSL_LOW, LSR_HIGH, LSR_LOW, MUL_HIGH,
       MUL_LOW, multiplexer_2_out, multiplexer_3_out, multiplexer_4_out, multiplexer_5_out, not_1_out,
       not_5_out, not_6_out, OR_LOW, ROTR_HIGH, ROTR_LOW, SUB_HIGH, SUB_LOW, undriven, undriven_2,
       undriven_3, undriven_4, undriven_5, undriven_6, XOR_LOW;

  assign not_1_out = ~b;  // NOT_Gate not_1, 32 bits wide
  Register #(.width(32)) a_Reg (.D(a), .clk(clk), .Q(a_Reg_q));  // open: en, clr
  Register #(.width(32)) b_Reg (.D(b), .clk(clk), .Q(b_Reg_q));  // open: en, clr
  Register #(.width(4)) aluop_Reg (.D(aluop), .clk(clk), .Q(aluop_Reg_q));  // open: en, clr
  CSA Sum (.a(a), .b(b), .s(ADD_LOW), .cout(ADD_HIGH[0]));  // open: cin
  CSA SUB (.cin(1'b1), .a(a), .b(not_1_out), .s(SUB_LOW), .cout(SUB_cout));
  not not_2 (not_2_out, comparator_1_eq);
  Comparator #(.width(32)) comparator_1 (.a(a_Reg_q), .b(a), .eq(comparator_1_eq));  // open: gt, lt
  not not_3 (not_3_out, comparator_2_eq);
  Comparator #(.width(32)) comparator_2 (.a(b_Reg_q), .b(b), .eq(comparator_2_eq));  // open: gt, lt
  not not_4 (not_4_out, comparator_3_eq);
  Comparator #(.width(4)) comparator_3 (.a(aluop_Reg_q), .b(aluop), .eq(comparator_3_eq));  // open: gt, lt
  Multiplexer #(.width(32)) multiplexer_1 (.in0({32{1'b1}}), .in1({32{1'b0}}), .out(SUB_HIGH), .sel(SUB_cout));
  LSR Logical_Shift_Right (.a(a), .b(b), .shifted({LSR_HIGH, LSR_LOW}));
  LSL Logical_Shift_Left (.a(a), .b(b), .shifted({LSL_HIGH, LSL_LOW}));
  CL_O CLO (.a(a), .num_Of_1({CLO_HIGH, CLO_LOW}));
  or or_1 (or_1_out, not_2_out, not_4_out, not_3_out);
  Comparator #(.width(4)) comparator_4 (.a(aluop), .b(4'b0010), .eq(comparator_4_eq));  // open: gt, lt
  Comparator #(.width(4)) comparator_5 (.a(aluop), .b(4'b0011), .eq(comparator_5_eq));  // open: gt, lt
  or or_2 (or_2_out, comparator_4_eq, comparator_5_eq);
  Multiplexer #(.select(4), .width(32)) multiplexer_2 (
    .in0(ADD_LOW), .in1(SUB_LOW), .in2(MUL_LOW), .in3(DIV_LOW), .in4(AND_LOW), .in5(OR_LOW), .in6(XOR_LOW),
    .in7(CLO_LOW), .in8(CLZ_LOW), .in9(LSL_LOW), .in10(LSR_LOW), .in11(ASR_LOW), .in12(ROTR_LOW),
    .in13(undriven_4), .in14(undriven_5), .in15(undriven_6), .out(multiplexer_2_out), .sel(aluop));
  Multiplexer #(.select(4), .width(32)) multiplexer_3 (
    .in0({{31{1'b0}}, ADD_HIGH[0]}), .in1(SUB_HIGH), .in2(MUL_HIGH), .in3(DIV_HIGH), .in4({32{1'b0}}),
    .in5({32{1'b0}}), .in6({32{1'b0}}), .in7(CLO_HIGH), .in8(CLZ_HIGH), .in9(LSL_HIGH), .in10(LSR_HIGH),
    .in11(ASR_HIGH), .in12(ROTR_HIGH), .in13(undriven), .in14(undriven_2), .in15(undriven_3),
    .out(multiplexer_3_out), .sel(aluop));
  and and_1 (start, or_1_out, or_2_out);
  assign not_5_out = ~multiplexer_2_out;  // NOT_Gate not_5, 32 bits wide
  Multiplexer #(.width(32)) multiplexer_4 (
    .in0(multiplexer_3_out), .in1(not_6_out), .out(multiplexer_4_out), .sel(output_inverted));
  assign not_6_out = ~multiplexer_3_out;  // NOT_Gate not_6, 32 bits wide
  Multiplexer #(.width(32)) multiplexer_5 (
    .in0(multiplexer_2_out), .in1(not_5_out), .out(multiplexer_5_out), .sel(output_inverted));
  Adder #(.width(32)) adder_1 (
    .a(multiplexer_4_out), .b({32{1'b0}}), .out(adder_1_out), .cin(adder_2_cout));  // open: cout
  mul Multiplier (.clk(clk), .start(start), .a(a), .b(b), .done(done_MULT), .Result({MUL_HIGH, MUL_LOW}));
  Div Divider (
    .start(start), .clk(clk), .dividend(a), .divisor(b), .done(done_DIV), .remainder(DIV_HIGH),
    .quotient(DIV_LOW));
  ASR Arithmetic_Shift_Right (.a(a), .b(b), .shifted({ASR_HIGH, ASR_LOW}));
  ROT_R Rotate_Right (.a(a), .b(b), .rotated({ROTR_HIGH, ROTR_LOW}));
  CL_Z CLZ (.a(a), .num_Of_0({CLZ_HIGH, CLZ_LOW}));
  Adder #(.width(32)) adder_2 (.a(multiplexer_5_out), .b(32'h1), .out(adder_2_out), .cout(adder_2_cout));  // open: cin
  Multiplexer #(.width(32)) multiplexer_6 (
    .in0(multiplexer_4_out), .in1(adder_1_out), .out(res_high), .sel(output_inc));
  Multiplexer #(.width(32)) multiplexer_7 (.in0(multiplexer_5_out), .in1(adder_2_out), .out(res_low), .sel(output_inc));
  assign AND_LOW = a & b;  // AND_Gate and_2, 32 bits wide
  assign OR_LOW = a | b;  // OR_Gate or_3, 32 bits wide
  assign XOR_LOW = a ^ b;  // XOR_Gate xor_1, 32 bits wide
  Multiplexer #(.select(4)) multiplexer_8 (
    .in0(1'b1), .in1(1'b1), .in2(done_MULT), .in3(done_DIV), .in4(1'b1), .in5(1'b1), .in6(1'b1), .in7(1'b1),
    .in8(1'b1), .in9(1'b1), .in10(1'b1), .in11(1'b1), .in12(1'b1), .in13(1'b1), .in14(1'b1), .in15(1'b1),
    .out(done), .sel(aluop));

  // Other names for the same wires on the sheet: inc = output_inc; invert = output_inverted
endmodule

module jtag_ram8 (
  input  clk,
  input  Jen,
  input  [31:0] Din,
  input  [31:0] Jin,
  input  Wen,
  input  [2:0] Addr,
  output [31:0] Dout,
  output [31:0] Jout
);

  wire decoder_1_out0, decoder_1_out1, decoder_1_out2, decoder_1_out3, decoder_1_out4, decoder_1_out5,
       decoder_1_out6, decoder_1_out7, or_1_out, or_2_out, or_3_out, or_4_out, or_5_out, or_6_out, or_7_out,
       or_8_out;
  wire [31:0] M0, M1, M2, M3, M4, M5, M6, multiplexer_1_out, multiplexer_2_out, multiplexer_3_out,
       multiplexer_4_out, multiplexer_5_out, multiplexer_6_out, multiplexer_7_out, multiplexer_8_out;

  Decoder #(.select(3)) decoder_1 (
    .out0(decoder_1_out0), .out1(decoder_1_out1), .out2(decoder_1_out2), .out3(decoder_1_out3),
    .out4(decoder_1_out4), .out5(decoder_1_out5), .out6(decoder_1_out6), .out7(decoder_1_out7), .sel(Addr),
    .en(Wen));
  Multiplexer #(.width(32)) multiplexer_1 (.in0(Din), .in1(Jin), .out(multiplexer_1_out), .sel(Jen));
  Multiplexer #(.width(32)) multiplexer_2 (.in0(Din), .in1(M0), .out(multiplexer_2_out), .sel(Jen));
  Multiplexer #(.width(32)) multiplexer_3 (.in0(Din), .in1(M1), .out(multiplexer_3_out), .sel(Jen));
  Multiplexer #(.width(32)) multiplexer_4 (.in0(Din), .in1(M2), .out(multiplexer_4_out), .sel(Jen));
  Multiplexer #(.width(32)) multiplexer_5 (.in0(Din), .in1(M3), .out(multiplexer_5_out), .sel(Jen));
  Multiplexer #(.width(32)) multiplexer_6 (.in0(Din), .in1(M4), .out(multiplexer_6_out), .sel(Jen));
  Multiplexer #(.width(32)) multiplexer_7 (.in0(Din), .in1(M5), .out(multiplexer_7_out), .sel(Jen));
  Multiplexer #(.width(32)) multiplexer_8 (.in0(Din), .in1(M6), .out(multiplexer_8_out), .sel(Jen));
  Register #(.width(32)) register_1 (.D(multiplexer_1_out), .en(or_1_out), .clk(clk), .Q(M0));  // open: clr
  or or_1 (or_1_out, Jen, decoder_1_out0);
  Register #(.width(32)) register_2 (.D(multiplexer_2_out), .en(or_2_out), .clk(clk), .Q(M1));  // open: clr
  or or_2 (or_2_out, Jen, decoder_1_out1);
  Register #(.width(32)) register_3 (.D(multiplexer_3_out), .en(or_3_out), .clk(clk), .Q(M2));  // open: clr
  or or_3 (or_3_out, Jen, decoder_1_out2);
  Register #(.width(32)) register_4 (.D(multiplexer_4_out), .en(or_4_out), .clk(clk), .Q(M3));  // open: clr
  or or_4 (or_4_out, Jen, decoder_1_out3);
  Register #(.width(32)) register_5 (.D(multiplexer_5_out), .en(or_5_out), .clk(clk), .Q(M4));  // open: clr
  or or_5 (or_5_out, Jen, decoder_1_out4);
  Register #(.width(32)) register_6 (.D(multiplexer_6_out), .en(or_6_out), .clk(clk), .Q(M5));  // open: clr
  or or_6 (or_6_out, Jen, decoder_1_out5);
  Register #(.width(32)) register_7 (.D(multiplexer_7_out), .en(or_7_out), .clk(clk), .Q(M6));  // open: clr
  or or_7 (or_7_out, Jen, decoder_1_out6);
  Register #(.width(32)) register_8 (.D(multiplexer_8_out), .en(or_8_out), .clk(clk), .Q(Jout));  // open: clr
  or or_8 (or_8_out, Jen, decoder_1_out7);
  Multiplexer #(.select(3), .width(32)) multiplexer_9 (
    .in0(M0), .in1(M1), .in2(M2), .in3(M3), .in4(M4), .in5(M5), .in6(M6), .in7(Jout), .out(Dout), .sel(Addr));

  // Other names for the same wires on the sheet: M7[31:0] = Jout
endmodule

module jtag_ram64 (
  input  clk,
  input  Jen,
  input  [31:0] Din,
  input  [31:0] Jin,
  input  Wen,
  input  [5:0] Addr,
  output [31:0] Dout,
  output [31:0] Jout
);

  wire decoder_1_out0, decoder_1_out1, decoder_1_out2, decoder_1_out3, decoder_1_out4, decoder_1_out5,
       decoder_1_out6, decoder_1_out7;
  wire [31:0] b0_dout, b0_jout, b1_dout, b1_jout, b2_dout, b2_jout, b3_dout, b3_jout, b4_dout, b4_jout,
       b5_dout, b5_jout, b6_dout, b6_jout, b7_dout;

  Decoder #(.select(3)) decoder_1 (
    .out0(decoder_1_out0), .out1(decoder_1_out1), .out2(decoder_1_out2), .out3(decoder_1_out3),
    .out4(decoder_1_out4), .out5(decoder_1_out5), .out6(decoder_1_out6), .out7(decoder_1_out7),
    .sel(Addr[5:3]), .en(Wen));
  jtag_ram8 b0 (
    .clk(clk), .Jen(Jen), .Din(Din), .Jin(Jin), .Wen(decoder_1_out0), .Addr(Addr[2:0]), .Dout(b0_dout),
    .Jout(b0_jout));
  jtag_ram8 b1 (
    .clk(clk), .Jen(Jen), .Din(Din), .Jin(b0_jout), .Wen(decoder_1_out1), .Addr(Addr[2:0]), .Dout(b1_dout),
    .Jout(b1_jout));
  jtag_ram8 b2 (
    .clk(clk), .Jen(Jen), .Din(Din), .Jin(b1_jout), .Wen(decoder_1_out2), .Addr(Addr[2:0]), .Dout(b2_dout),
    .Jout(b2_jout));
  jtag_ram8 b3 (
    .clk(clk), .Jen(Jen), .Din(Din), .Jin(b2_jout), .Wen(decoder_1_out3), .Addr(Addr[2:0]), .Dout(b3_dout),
    .Jout(b3_jout));
  jtag_ram8 b4 (
    .clk(clk), .Jen(Jen), .Din(Din), .Jin(b3_jout), .Wen(decoder_1_out4), .Addr(Addr[2:0]), .Dout(b4_dout),
    .Jout(b4_jout));
  jtag_ram8 b5 (
    .clk(clk), .Jen(Jen), .Din(Din), .Jin(b4_jout), .Wen(decoder_1_out5), .Addr(Addr[2:0]), .Dout(b5_dout),
    .Jout(b5_jout));
  jtag_ram8 b6 (
    .clk(clk), .Jen(Jen), .Din(Din), .Jin(b5_jout), .Wen(decoder_1_out6), .Addr(Addr[2:0]), .Dout(b6_dout),
    .Jout(b6_jout));
  jtag_ram8 b7 (
    .clk(clk), .Jen(Jen), .Din(Din), .Jin(b6_jout), .Wen(decoder_1_out7), .Addr(Addr[2:0]), .Dout(b7_dout),
    .Jout(Jout));
  Multiplexer #(.select(3), .width(32)) multiplexer_1 (
    .in0(b0_dout), .in1(b1_dout), .in2(b2_dout), .in3(b3_dout), .in4(b4_dout), .in5(b5_dout), .in6(b6_dout),
    .in7(b7_dout), .out(Dout), .sel(Addr[5:3]));
endmodule

module jtag_ram512 (
  input  clk,
  input  Jen,
  input  [31:0] Din,
  input  [31:0] Jin,
  input  Wen,
  input  [8:0] Addr,
  output [31:0] Jout,
  output [31:0] Dout
);

  wire decoder_1_out0, decoder_1_out1, decoder_1_out2, decoder_1_out3, decoder_1_out4, decoder_1_out5,
       decoder_1_out6, decoder_1_out7;
  wire [31:0] b0_dout, b0_jout, b1_dout, b1_jout, b2_dout, b2_jout, b3_dout, b3_jout, b4_dout, b4_jout,
       b5_dout, b5_jout, b6_dout, b6_jout, b7_dout;

  Decoder #(.select(3)) decoder_1 (
    .out0(decoder_1_out0), .out1(decoder_1_out1), .out2(decoder_1_out2), .out3(decoder_1_out3),
    .out4(decoder_1_out4), .out5(decoder_1_out5), .out6(decoder_1_out6), .out7(decoder_1_out7),
    .sel(Addr[8:6]), .en(Wen));
  jtag_ram64 b0 (
    .clk(clk), .Jen(Jen), .Din(Din), .Jin(Jin), .Wen(decoder_1_out0), .Addr(Addr[5:0]), .Dout(b0_dout),
    .Jout(b0_jout));
  jtag_ram64 b1 (
    .clk(clk), .Jen(Jen), .Din(Din), .Jin(b0_jout), .Wen(decoder_1_out1), .Addr(Addr[5:0]), .Dout(b1_dout),
    .Jout(b1_jout));
  jtag_ram64 b2 (
    .clk(clk), .Jen(Jen), .Din(Din), .Jin(b1_jout), .Wen(decoder_1_out2), .Addr(Addr[5:0]), .Dout(b2_dout),
    .Jout(b2_jout));
  jtag_ram64 b3 (
    .clk(clk), .Jen(Jen), .Din(Din), .Jin(b2_jout), .Wen(decoder_1_out3), .Addr(Addr[5:0]), .Dout(b3_dout),
    .Jout(b3_jout));
  jtag_ram64 b4 (
    .clk(clk), .Jen(Jen), .Din(Din), .Jin(b3_jout), .Wen(decoder_1_out4), .Addr(Addr[5:0]), .Dout(b4_dout),
    .Jout(b4_jout));
  jtag_ram64 b5 (
    .clk(clk), .Jen(Jen), .Din(Din), .Jin(b4_jout), .Wen(decoder_1_out5), .Addr(Addr[5:0]), .Dout(b5_dout),
    .Jout(b5_jout));
  jtag_ram64 b6 (
    .clk(clk), .Jen(Jen), .Din(Din), .Jin(b5_jout), .Wen(decoder_1_out6), .Addr(Addr[5:0]), .Dout(b6_dout),
    .Jout(b6_jout));
  jtag_ram64 b7 (
    .clk(clk), .Jen(Jen), .Din(Din), .Jin(b6_jout), .Wen(decoder_1_out7), .Addr(Addr[5:0]), .Dout(b7_dout),
    .Jout(Jout));
  Multiplexer #(.select(3), .width(32)) multiplexer_1 (
    .in0(b0_dout), .in1(b1_dout), .in2(b2_dout), .in3(b3_dout), .in4(b4_dout), .in5(b5_dout), .in6(b6_dout),
    .in7(b7_dout), .out(Dout), .sel(Addr[8:6]));
endmodule

module regfile (
  input  clk,
  input  rst,
  input  [31:0] Dwrite,
  input  [4:0] Awrite,
  input  [4:0] Aread0,
  input  [4:0] Aread1,
  output [31:0] Dread0,
  output [31:0] Dread1,
  output [31:0] R1,
  output [31:0] R2,
  output [31:0] R3,
  output [31:0] R4,
  output [31:0] R5,
  output [31:0] R6,
  output [31:0] R7,
  output [31:0] R8,
  output [31:0] R9,
  output [31:0] R10,
  output [31:0] R11,
  output [31:0] R12,
  output [31:0] R13,
  output [31:0] R14,
  output [31:0] R15,
  output [31:0] R16,
  output [31:0] R17,
  output [31:0] R18,
  output [31:0] R19,
  output [31:0] R20,
  output [31:0] R21,
  output [31:0] R22,
  output [31:0] R23,
  output [31:0] R24,
  output [31:0] R25,
  output [31:0] R26,
  output [31:0] R27,
  output [31:0] R28,
  output [31:0] R29,
  output [31:0] R30,
  output [31:0] R31
);

  wire and_1_out, and_2_out, and_3_out, and_4_out, and_5_out, and_6_out, and_7_out, and_8_out, and_9_out,
       and_10_out, and_11_out, and_12_out, and_13_out, and_14_out, and_15_out, and_16_out, and_17_out,
       and_18_out, and_19_out, and_20_out, and_21_out, and_22_out, and_23_out, and_24_out, and_25_out,
       and_26_out, and_27_out, and_28_out, and_29_out, and_30_out, and_31_out, and_32_out, decoder_1_out0,
       decoder_1_out1, decoder_1_out2, decoder_1_out3, decoder_1_out4, decoder_1_out5, decoder_1_out6,
       decoder_1_out7, decoder_2_out0, decoder_2_out1, decoder_2_out2, decoder_2_out3, or_1_out, or_2_out,
       or_3_out, or_4_out, or_5_out, or_6_out, or_7_out, or_8_out, or_9_out, or_10_out, or_11_out, or_12_out,
       or_13_out, or_14_out, or_15_out, or_16_out, or_17_out, or_18_out, or_19_out, or_20_out, or_21_out,
       or_22_out, or_23_out, or_24_out, or_25_out, or_26_out, or_27_out, or_28_out, or_29_out, or_30_out,
       or_31_out, or_32_out, undriven_2, undriven_3, undriven_4, undriven_5;
  wire [31:0] multiplexer_1_out, multiplexer_2_out, multiplexer_3_out, multiplexer_4_out, multiplexer_5_out,
       multiplexer_6_out, multiplexer_7_out, multiplexer_8_out, multiplexer_9_out, undriven;

  Register #(.width(32)) register_1 (.D(undriven), .en(or_1_out), .clk(undriven_2));  // open: Q, clr
  or or_1 (or_1_out, undriven_5, and_1_out);
  and and_1 (and_1_out, undriven_4, undriven_3);
  Decoder #(.select(3)) decoder_1 (
    .out0(decoder_1_out0), .out1(decoder_1_out1), .out2(decoder_1_out2), .out3(decoder_1_out3),
    .out4(decoder_1_out4), .out5(decoder_1_out5), .out6(decoder_1_out6), .out7(decoder_1_out7),
    .sel(Awrite[4:2]));  // open: en
  Decoder #(.select(2)) decoder_2 (
    .out0(decoder_2_out0), .out1(decoder_2_out1), .out2(decoder_2_out2), .out3(decoder_2_out3),
    .sel(Awrite[1:0]));  // open: en
  Multiplexer #(.width(32)) multiplexer_1 (.in0(Dwrite), .in1({32{1'b0}}), .out(multiplexer_1_out), .sel(rst));
  and and_2 (and_2_out, decoder_2_out0, decoder_1_out1);
  and and_3 (and_3_out, decoder_2_out0, decoder_1_out2);
  and and_4 (and_4_out, decoder_2_out0, decoder_1_out3);
  and and_5 (and_5_out, decoder_2_out0, decoder_1_out4);
  and and_6 (and_6_out, decoder_2_out0, decoder_1_out5);
  and and_7 (and_7_out, decoder_2_out0, decoder_1_out6);
  and and_8 (and_8_out, decoder_2_out0, decoder_1_out7);
  Register #(.width(32)) register_2 (.D(multiplexer_1_out), .en(or_2_out), .clk(clk), .Q(R4));  // open: clr
  or or_2 (or_2_out, rst, and_2_out);
  Register #(.width(32)) register_3 (.D(multiplexer_1_out), .en(or_3_out), .clk(clk), .Q(R8));  // open: clr
  or or_3 (or_3_out, rst, and_3_out);
  Register #(.width(32)) register_4 (.D(multiplexer_1_out), .en(or_4_out), .clk(clk), .Q(R12));  // open: clr
  or or_4 (or_4_out, rst, and_4_out);
  Register #(.width(32)) register_5 (.D(multiplexer_1_out), .en(or_5_out), .clk(clk), .Q(R16));  // open: clr
  or or_5 (or_5_out, rst, and_5_out);
  Register #(.width(32)) register_6 (.D(multiplexer_1_out), .en(or_6_out), .clk(clk), .Q(R20));  // open: clr
  or or_6 (or_6_out, rst, and_6_out);
  Register #(.width(32)) register_7 (.D(multiplexer_1_out), .en(or_7_out), .clk(clk), .Q(R24));  // open: clr
  or or_7 (or_7_out, rst, and_7_out);
  Register #(.width(32)) register_8 (.D(multiplexer_1_out), .en(or_8_out), .clk(clk), .Q(R28));  // open: clr
  or or_8 (or_8_out, rst, and_8_out);
  Multiplexer #(.select(3), .width(32)) multiplexer_2 (
    .in0({32{1'b0}}), .in1(R4), .in2(R8), .in3(R12), .in4(R16), .in5(R20), .in6(R24), .in7(R28),
    .out(multiplexer_2_out), .sel(Aread0[4:2]));
  Multiplexer #(.select(3), .width(32)) multiplexer_3 (
    .in0({32{1'b0}}), .in1(R4), .in2(R8), .in3(R12), .in4(R16), .in5(R20), .in6(R24), .in7(R28),
    .out(multiplexer_3_out), .sel(Aread1[4:2]));
  and and_9 (and_9_out, decoder_2_out1, decoder_1_out0);
  and and_10 (and_10_out, decoder_2_out1, decoder_1_out1);
  and and_11 (and_11_out, decoder_2_out1, decoder_1_out2);
  and and_12 (and_12_out, decoder_2_out1, decoder_1_out3);
  and and_13 (and_13_out, decoder_2_out1, decoder_1_out4);
  and and_14 (and_14_out, decoder_2_out1, decoder_1_out5);
  and and_15 (and_15_out, decoder_2_out1, decoder_1_out6);
  and and_16 (and_16_out, decoder_2_out1, decoder_1_out7);
  Register #(.width(32)) register_9 (.D(multiplexer_1_out), .en(or_9_out), .clk(clk), .Q(R1));  // open: clr
  or or_9 (or_9_out, rst, and_9_out);
  Register #(.width(32)) register_10 (.D(multiplexer_1_out), .en(or_10_out), .clk(clk), .Q(R5));  // open: clr
  or or_10 (or_10_out, rst, and_10_out);
  Register #(.width(32)) register_11 (.D(multiplexer_1_out), .en(or_11_out), .clk(clk), .Q(R9));  // open: clr
  or or_11 (or_11_out, rst, and_11_out);
  Register #(.width(32)) register_12 (.D(multiplexer_1_out), .en(or_12_out), .clk(clk), .Q(R13));  // open: clr
  or or_12 (or_12_out, rst, and_12_out);
  Register #(.width(32)) register_13 (.D(multiplexer_1_out), .en(or_13_out), .clk(clk), .Q(R17));  // open: clr
  or or_13 (or_13_out, rst, and_13_out);
  Register #(.width(32)) register_14 (.D(multiplexer_1_out), .en(or_14_out), .clk(clk), .Q(R21));  // open: clr
  or or_14 (or_14_out, rst, and_14_out);
  Register #(.width(32)) register_15 (.D(multiplexer_1_out), .en(or_15_out), .clk(clk), .Q(R25));  // open: clr
  or or_15 (or_15_out, rst, and_15_out);
  Register #(.width(32)) register_16 (.D(multiplexer_1_out), .en(or_16_out), .clk(clk), .Q(R29));  // open: clr
  or or_16 (or_16_out, rst, and_16_out);
  Multiplexer #(.select(3), .width(32)) multiplexer_4 (
    .in0(R1), .in1(R5), .in2(R9), .in3(R13), .in4(R17), .in5(R21), .in6(R25), .in7(R29),
    .out(multiplexer_4_out), .sel(Aread0[4:2]));
  Multiplexer #(.select(3), .width(32)) multiplexer_5 (
    .in0(R1), .in1(R5), .in2(R9), .in3(R13), .in4(R17), .in5(R21), .in6(R25), .in7(R29),
    .out(multiplexer_5_out), .sel(Aread1[4:2]));
  Register #(.width(32)) register_17 (.D(multiplexer_1_out), .en(or_17_out), .clk(clk), .Q(R2));  // open: clr
  or or_17 (or_17_out, rst, and_17_out);
  and and_17 (and_17_out, decoder_2_out2, decoder_1_out0);
  Register #(.width(32)) register_18 (.D(multiplexer_1_out), .en(or_18_out), .clk(clk), .Q(R6));  // open: clr
  or or_18 (or_18_out, rst, and_18_out);
  and and_18 (and_18_out, decoder_2_out2, decoder_1_out1);
  Register #(.width(32)) register_19 (.D(multiplexer_1_out), .en(or_19_out), .clk(clk), .Q(R10));  // open: clr
  or or_19 (or_19_out, rst, and_19_out);
  and and_19 (and_19_out, decoder_2_out2, decoder_1_out2);
  Register #(.width(32)) register_20 (.D(multiplexer_1_out), .en(or_20_out), .clk(clk), .Q(R14));  // open: clr
  or or_20 (or_20_out, rst, and_20_out);
  and and_20 (and_20_out, decoder_2_out2, decoder_1_out3);
  Register #(.width(32)) register_21 (.D(multiplexer_1_out), .en(or_21_out), .clk(clk), .Q(R18));  // open: clr
  or or_21 (or_21_out, rst, and_21_out);
  and and_21 (and_21_out, decoder_2_out2, decoder_1_out4);
  Register #(.width(32)) register_22 (.D(multiplexer_1_out), .en(or_22_out), .clk(clk), .Q(R22));  // open: clr
  or or_22 (or_22_out, rst, and_22_out);
  and and_22 (and_22_out, decoder_2_out2, decoder_1_out5);
  Register #(.width(32)) register_23 (.D(multiplexer_1_out), .en(or_23_out), .clk(clk), .Q(R26));  // open: clr
  or or_23 (or_23_out, rst, and_23_out);
  and and_23 (and_23_out, decoder_2_out2, decoder_1_out6);
  Register #(.width(32)) register_24 (.D(multiplexer_1_out), .en(or_24_out), .clk(clk), .Q(R30));  // open: clr
  or or_24 (or_24_out, rst, and_24_out);
  and and_24 (and_24_out, decoder_2_out2, decoder_1_out7);
  Multiplexer #(.select(3), .width(32)) multiplexer_6 (
    .in0(R2), .in1(R6), .in2(R10), .in3(R14), .in4(R18), .in5(R22), .in6(R26), .in7(R30),
    .out(multiplexer_6_out), .sel(Aread0[4:2]));
  Multiplexer #(.select(3), .width(32)) multiplexer_7 (
    .in0(R2), .in1(R6), .in2(R10), .in3(R14), .in4(R18), .in5(R22), .in6(R26), .in7(R30),
    .out(multiplexer_7_out), .sel(Aread1[4:2]));
  Register #(.width(32)) register_25 (.D(multiplexer_1_out), .en(or_25_out), .clk(clk), .Q(R3));  // open: clr
  or or_25 (or_25_out, rst, and_25_out);
  and and_25 (and_25_out, decoder_2_out3, decoder_1_out0);
  Register #(.width(32)) register_26 (.D(multiplexer_1_out), .en(or_26_out), .clk(clk), .Q(R7));  // open: clr
  or or_26 (or_26_out, rst, and_26_out);
  and and_26 (and_26_out, decoder_2_out3, decoder_1_out1);
  Register #(.width(32)) register_27 (.D(multiplexer_1_out), .en(or_27_out), .clk(clk), .Q(R11));  // open: clr
  or or_27 (or_27_out, rst, and_27_out);
  and and_27 (and_27_out, decoder_2_out3, decoder_1_out2);
  Register #(.width(32)) register_28 (.D(multiplexer_1_out), .en(or_28_out), .clk(clk), .Q(R15));  // open: clr
  or or_28 (or_28_out, rst, and_28_out);
  and and_28 (and_28_out, decoder_2_out3, decoder_1_out3);
  Register #(.width(32)) register_29 (.D(multiplexer_1_out), .en(or_29_out), .clk(clk), .Q(R19));  // open: clr
  or or_29 (or_29_out, rst, and_29_out);
  and and_29 (and_29_out, decoder_2_out3, decoder_1_out4);
  Register #(.width(32)) register_30 (.D(multiplexer_1_out), .en(or_30_out), .clk(clk), .Q(R23));  // open: clr
  or or_30 (or_30_out, rst, and_30_out);
  and and_30 (and_30_out, decoder_2_out3, decoder_1_out5);
  Register #(.width(32)) register_31 (.D(multiplexer_1_out), .en(or_31_out), .clk(clk), .Q(R27));  // open: clr
  or or_31 (or_31_out, rst, and_31_out);
  and and_31 (and_31_out, decoder_2_out3, decoder_1_out6);
  Register #(.width(32)) register_32 (.D(multiplexer_1_out), .en(or_32_out), .clk(clk), .Q(R31));  // open: clr
  or or_32 (or_32_out, rst, and_32_out);
  and and_32 (and_32_out, decoder_2_out3, decoder_1_out7);
  Multiplexer #(.select(3), .width(32)) multiplexer_8 (
    .in0(R3), .in1(R7), .in2(R11), .in3(R15), .in4(R19), .in5(R23), .in6(R27), .in7(R31),
    .out(multiplexer_8_out), .sel(Aread0[4:2]));
  Multiplexer #(.select(3), .width(32)) multiplexer_9 (
    .in0(R3), .in1(R7), .in2(R11), .in3(R15), .in4(R19), .in5(R23), .in6(R27), .in7(R31),
    .out(multiplexer_9_out), .sel(Aread1[4:2]));
  Multiplexer #(.select(2), .width(32)) multiplexer_10 (
    .in0(multiplexer_2_out), .in1(multiplexer_4_out), .in2(multiplexer_6_out), .in3(multiplexer_8_out),
    .out(Dread0), .sel(Aread0[1:0]));
  Multiplexer #(.select(2), .width(32)) multiplexer_11 (
    .in0(multiplexer_3_out), .in1(multiplexer_5_out), .in2(multiplexer_7_out), .in3(multiplexer_9_out),
    .out(Dread1), .sel(Aread1[1:0]));

  // Notes on the sheet:
  //   Field Template
endmodule

module counter2 (
  input  clk,
  input  reset,
  output num
);

  wire adder_1_out;

  Adder #(.width(1)) adder_1 (.a(num), .b(1'b1), .out(adder_1_out));  // open: cin, cout
  Register #(.width(1)) register_1 (.D(adder_1_out), .clk(clk), .Q(num), .clr(reset));  // open: en
endmodule

module Div (
  input  start,
  input  clk,
  input  [31:0] dividend,
  input  [31:0] divisor,
  output done,
  output [31:0] remainder,
  output [31:0] quotient
);

  wire comparator_1_gt, comparator_2_lt, counter_div_num, not_1_out, not_3_out, undriven;
  wire [7:0] adder_1_out, counter_q;
  wire [31:0] adder_2_out, multiplexer_1_out, multiplexer_2_out, multiplexer_3_out, multiplexer_4_out,
       multiplexer_5_out, shifter_1_out, shifter_1_out_2, subtractor_1_out;
  wire [63:0] q_q;

  not not_1 (not_1_out, counter_div_num);
  Multiplexer #(.width(32)) multiplexer_1 (
    .in0(q_q[31:0]), .in1(adder_2_out), .out(multiplexer_1_out), .sel(not_3_out));
  Adder adder_1 (.a(counter_q), .b(8'h1), .out(adder_1_out));  // open: cin, cout
  Register counter (.D(adder_1_out), .en(not_1_out), .clk(clk), .Q(counter_q), .clr(start));
  Multiplexer #(.width(32)) multiplexer_2 (
    .in0(shifter_1_out_2), .in1(multiplexer_3_out), .out(multiplexer_2_out), .sel(counter_div_num));
  Multiplexer #(.width(32)) multiplexer_3 (
    .in0(q_q[63:32]), .in1(subtractor_1_out), .out(multiplexer_3_out), .sel(not_3_out));
  Multiplexer #(.width(32)) multiplexer_4 (
    .in0(shifter_1_out), .in1(multiplexer_1_out), .out(multiplexer_4_out), .sel(counter_div_num));
  Multiplexer #(.width(32)) multiplexer_5 (
    .in0(multiplexer_4_out), .in1(dividend), .out(multiplexer_5_out), .sel(start));
  Register #(.width(32)) a (.D(multiplexer_2_out), .en(done), .clk(clk), .Q(q_q[63:32]), .clr(start));
  Register #(.width(32)) q (.D(multiplexer_5_out), .en(done), .clk(clk), .Q(q_q[31:0]), .clr(undriven));
  counter2 counter_div (.clk(clk), .reset(start), .num(counter_div_num));
  Comparator comparator_1 (.a(counter_q), .b(8'h20), .gt(comparator_1_gt));  // open: eq, lt
  Comparator #(.mode("unsigned"), .width(32)) comparator_2 (
    .a(q_q[63:32]), .b(divisor), .lt(comparator_2_lt));  // open: gt, eq
  not not_2 (done, comparator_1_gt);
  Shifter #(.width(64)) shifter_1 (.in(q_q), .\dist (6'b000001), .out({shifter_1_out_2, shifter_1_out}));
  not not_3 (not_3_out, comparator_2_lt);
  Register #(.width(32)) register_1 (.D(q_q[63:32]), .en(done), .clk(clk), .Q(remainder));  // open: clr
  Subtractor #(.width(32)) subtractor_1 (.a(q_q[63:32]), .b(divisor), .out(subtractor_1_out));  // open: bin, bout
  Adder #(.width(32)) adder_2 (.a(q_q[31:0]), .b(32'h1), .out(adder_2_out));  // open: cin, cout
  Register #(.width(32)) register_2 (.D(q_q[31:0]), .en(done), .clk(clk), .Q(quotient));  // open: clr
endmodule

module CSA (
  input  cin,
  input  [31:0] a,
  input  [31:0] b,
  output [31:0] s,
  output cout
);

  wire adder_1_cout, adder_2_cout, adder_3_cout, adder_4_cout, adder_5_cout, adder_6_cout, adder_7_cout,
       multiplexer_2_out, multiplexer_3_out;
  wire [7:0] adder_2_out, adder_3_out, adder_4_out, adder_5_out, adder_6_out, adder_7_out;

  Adder adder_1 (.a(a[7:0]), .b(b[7:0]), .out(s[7:0]), .cin(cin), .cout(adder_1_cout));
  Adder adder_2 (.a(a[15:8]), .b(b[15:8]), .out(adder_2_out), .cout(adder_2_cout));  // open: cin
  Adder adder_3 (.a(a[15:8]), .b(b[15:8]), .out(adder_3_out), .cin(1'b1), .cout(adder_3_cout));
  Adder adder_4 (.a(a[23:16]), .b(b[23:16]), .out(adder_4_out), .cout(adder_4_cout));  // open: cin
  Adder adder_5 (.a(a[23:16]), .b(b[23:16]), .out(adder_5_out), .cin(1'b1), .cout(adder_5_cout));
  Adder adder_6 (.a(a[31:24]), .b(b[31:24]), .out(adder_6_out), .cout(adder_6_cout));  // open: cin
  Adder adder_7 (.a(a[31:24]), .b(b[31:24]), .out(adder_7_out), .cin(1'b1), .cout(adder_7_cout));
  Multiplexer #(.width(8)) multiplexer_1 (.in0(adder_2_out), .in1(adder_3_out), .out(s[15:8]), .sel(adder_1_cout));
  Multiplexer multiplexer_2 (.in0(adder_2_cout), .in1(adder_3_cout), .out(multiplexer_2_out), .sel(adder_1_cout));
  Multiplexer multiplexer_3 (.in0(adder_4_cout), .in1(adder_5_cout), .out(multiplexer_3_out), .sel(multiplexer_2_out));
  Multiplexer #(.width(8)) multiplexer_4 (
    .in0(adder_6_out), .in1(adder_7_out), .out(s[31:24]), .sel(multiplexer_3_out));
  Multiplexer multiplexer_5 (.in0(adder_6_cout), .in1(adder_7_cout), .out(cout), .sel(multiplexer_3_out));
  Multiplexer #(.width(8)) multiplexer_6 (
    .in0(adder_4_out), .in1(adder_5_out), .out(s[23:16]), .sel(multiplexer_2_out));
endmodule

module CsaveA (
  input  cin,
  input  [31:0] a,
  input  [31:0] b,
  input  [31:0] c,
  output [31:0] s,
  output COUT2,
  output COUT1,
  output COUT0
);

  wire CSAAdder_cout;
  wire [31:0] adders_cout, adders_s, shifter_1_out;

  Parallel_FullAdders adders (.a(a), .b(b), .cin(c), .s(adders_s), .cout(adders_cout));
  Shifter #(.width(32)) shifter_1 (.in(adders_cout), .\dist (5'b00001), .out(shifter_1_out));
  CSA CSAAdder (.cin(cin), .a(adders_s), .b(shifter_1_out), .s(s), .cout(CSAAdder_cout));
  and and_1 (COUT2, CSAAdder_cout, adders_cout[31]);
  xor xor_1 (COUT1, CSAAdder_cout, adders_cout[31]);
  nor nor_1 (COUT0, CSAAdder_cout, adders_cout[31]);
endmodule

module Parallel_FullAdders (
  input  [31:0] a,
  input  [31:0] b,
  input  [31:0] cin,
  output [31:0] s,
  output [31:0] cout
);

  wire [31:0] and_1_out, and_2_out, xor_1_out;

  assign and_1_out = a & b;  // AND_Gate and_1, 32 bits wide
  assign xor_1_out = a ^ b;  // XOR_Gate xor_1, 32 bits wide
  assign and_2_out = xor_1_out & cin;  // AND_Gate and_2, 32 bits wide
  assign s = xor_1_out ^ cin;  // XOR_Gate xor_2, 32 bits wide
  assign cout = and_2_out | and_1_out;  // OR_Gate or_1, 32 bits wide
endmodule

module mul (
  input  clk,
  input  start,
  input  [31:0] a,
  input  [31:0] b,
  output done,
  output [63:0] Result
);

  wire and_1_out, comparator_1_gt, comparator_1_lt, comparator_2_lt, comparator_3_lt, CSA_cout1, CSA_cout2,
       Init, nor_1_out, not_1_out, not_2_out, not_4_out, Opperation, or_1_out, or_2_out, or_3_out, or_4_out,
       or_5_out, OR_R1_FLAG, RE_q, RE_signal, sign, signal_1, signal_2, undriven;
  wire [31:0] adder_1_out, adder_3_out, adder_4_out, CSA2_s, CSA_s, IN1, IN2, multiplexer_1_out,
       multiplexer_2_out, multiplexer_3_out, multiplexer_4_out, multiplexer_5_out, multiplexer_6_out,
       not_5_out, not_6_out, R1_q, R2_q, R2_q_2, shifter_1_out, shifter_3_out;
  wire [63:0] adder_2_out, multiplexer_7_out, multiplexer_8_out, not_3_out, R3_q, shifter_2_out,
       shifter_4_out;

  not not_1 (not_1_out, OR_R1_FLAG);
  Multiplexer #(.width(32)) multiplexer_1 (
    .in0({32{1'b0}}), .in1(shifter_2_out[31:0]), .out(multiplexer_1_out), .sel(shifter_1_out[0]));
  Multiplexer #(.width(32)) multiplexer_2 (.in0({32{1'b0}}), .in1(R2_q_2), .out(multiplexer_2_out), .sel(R1_q[0]));
  Multiplexer #(.width(32)) multiplexer_3 (
    .in0({32{1'b0}}), .in1(shifter_2_out[63:32]), .out(multiplexer_3_out), .sel(shifter_1_out[0]));
  nor nor_1 (nor_1_out, Opperation, start);
  and and_1 (and_1_out, not_1_out, Opperation);
  Multiplexer #(.width(32)) multiplexer_4 (.in0({32{1'b0}}), .in1(R2_q), .out(multiplexer_4_out), .sel(R1_q[0]));
  and and_2 (signal_1, Init, start);
  Shifter #(.shift("lr"), .width(32)) shifter_1 (.in(R1_q), .\dist (5'b00001), .out(shifter_1_out));
  or or_1 (or_1_out, nor_1_out, and_1_out);
  and and_3 (signal_2, OR_R1_FLAG, Opperation);
  D_Flip_Flop u_Init (.D(or_1_out), .clk(clk), .Q(Init), .preset(start));  // open: Qn, reset
  D_Flip_Flop u_Opperation (.D(or_2_out), .clk(clk), .Q(Opperation), .reset(undriven));  // open: Qn, preset
  or or_2 (or_2_out, signal_1, signal_2);
  Shifter #(.width(64)) shifter_2 (.in({R2_q_2, R2_q}), .\dist (6'b000001), .out(shifter_2_out));
  CsaveA CSA (
    .a(multiplexer_4_out), .b(multiplexer_1_out), .c(R3_q[31:0]), .s(CSA_s), .COUT2(CSA_cout2),
    .COUT1(CSA_cout1));  // open: cin, COUT0
  CsaveA CSA2 (
    .cin(or_3_out), .a(multiplexer_2_out), .b(multiplexer_3_out), .c(R3_q[63:32]), .s(CSA2_s));  // open: COUT2, COUT1, COUT0
  Shifter #(.shift("lr"), .width(32)) shifter_3 (.in(shifter_1_out), .\dist (5'b00001), .out(shifter_3_out));
  Shifter #(.width(64)) shifter_4 (.in(shifter_2_out), .\dist (6'b000001), .out(shifter_4_out));
  or or_3 (or_3_out, CSA_cout2, CSA_cout1);
  Multiplexer #(.width(32)) multiplexer_5 (.in0(CSA2_s), .in1(adder_1_out), .out(multiplexer_5_out), .sel(CSA_cout2));
  Adder #(.width(32)) adder_1 (.a(CSA2_s), .b(32'h1), .out(adder_1_out));  // open: cin, cout
  and and_4 (RE_signal, Opperation, not_2_out);
  not not_2 (not_2_out, OR_R1_FLAG);
  Multiplexer #(.width(32)) multiplexer_6 (.in0(shifter_3_out), .in1(IN1), .out(multiplexer_6_out), .sel(signal_1));
  or or_4 (or_4_out, signal_1, signal_2);
  Multiplexer #(.width(64)) multiplexer_7 (
    .in0({{32{1'b0}}, IN2}), .in1(shifter_4_out), .out(multiplexer_7_out), .sel(signal_2));
  or or_5 (or_5_out, RE_signal, signal_1);
  Multiplexer #(.width(64)) multiplexer_8 (
    .in0({64{1'b0}}), .in1({multiplexer_5_out, CSA_s}), .out(multiplexer_8_out), .sel(signal_2));
  assign not_3_out = ~R3_q;  // NOT_Gate not_3, 64 bits wide
  Adder #(.width(64)) adder_2 (.a(not_3_out), .b(64'h1), .out(adder_2_out));  // open: cin, cout
  Register #(.width(32)) R1 (.D(multiplexer_6_out), .en(or_4_out), .clk(clk), .Q(R1_q));  // open: clr
  Register #(.width(64)) R2 (.D(multiplexer_7_out), .en(or_4_out), .clk(clk), .Q({R2_q_2, R2_q}));  // open: clr
  Register #(.width(64)) R3 (.D(multiplexer_8_out), .en(or_4_out), .clk(clk), .Q(R3_q));  // open: clr
  Register #(.width(1)) RE (.D(RE_signal), .en(or_5_out), .clk(clk), .Q(RE_q));  // open: clr
  Multiplexer #(.width(64)) multiplexer_9 (.in0(R3_q), .in1(adder_2_out), .out(Result), .sel(sign));
  not not_4 (not_4_out, done);
  or or_6 (done, RE_q, RE_signal);
  assign not_5_out = ~a;  // NOT_Gate not_5, 32 bits wide
  assign not_6_out = ~b;  // NOT_Gate not_6, 32 bits wide
  Comparator #(.width(32)) comparator_1 (
    .a(R1_q), .b({32{1'b0}}), .gt(comparator_1_gt), .lt(comparator_1_lt));  // open: eq
  Adder #(.width(32)) adder_3 (.a(not_5_out), .b(32'h1), .out(adder_3_out));  // open: cin, cout
  Comparator #(.width(32)) comparator_2 (.a(a), .b({32{1'b0}}), .lt(comparator_2_lt));  // open: gt, eq
  Adder #(.width(32)) adder_4 (.a(not_6_out), .b(32'h1), .out(adder_4_out));  // open: cin, cout
  Comparator #(.width(32)) comparator_3 (.a(b), .b({32{1'b0}}), .lt(comparator_3_lt));  // open: gt, eq
  or or_7 (OR_R1_FLAG, comparator_1_gt, comparator_1_lt);
  Multiplexer #(.width(32)) multiplexer_10 (.in0(a), .in1(adder_3_out), .out(IN1), .sel(comparator_2_lt));
  Multiplexer #(.width(32)) multiplexer_11 (.in0(b), .in1(adder_4_out), .out(IN2), .sel(comparator_3_lt));
  xor xor_1 (sign, comparator_2_lt, comparator_3_lt);

  // Other names for the same wires on the sheet: INN1[31:0] = a; INN2[31:0] = b; S = start
endmodule

module LSR (
  input  [31:0] a,
  input  [31:0] b,
  output [63:0] shifted
);

  wire comparator_1_eq, not_1_out;
  wire [31:0] multiplexer_1_out, subtractor_1_out;
  wire [63:0] multiplexer_2_out, shifter_1_out, shifter_2_out;

  Subtractor #(.width(32)) subtractor_1 (.a(b), .b(32'h1), .out(subtractor_1_out));  // open: bin, bout
  Multiplexer #(.width(32)) multiplexer_1 (.in0(subtractor_1_out), .in1(b), .out(multiplexer_1_out), .sel(b[0]));
  Comparator #(.width(5)) comparator_1 (.a(b[4:0]), .b({5{1'b0}}), .eq(comparator_1_eq));  // open: gt, lt
  Shifter #(.shift("lr"), .width(64)) shifter_1 (
    .in({{32{1'b0}}, a}), .\dist ({1'b0, multiplexer_1_out[4:0]}), .out(shifter_1_out));
  not not_1 (not_1_out, b[0]);
  Shifter #(.shift("lr"), .width(64)) shifter_2 (.in(shifter_1_out), .\dist (6'b000001), .out(shifter_2_out));
  Multiplexer #(.width(64)) multiplexer_2 (
    .in0(shifter_1_out), .in1(shifter_2_out), .out(multiplexer_2_out), .sel(not_1_out));
  Multiplexer #(.width(64)) multiplexer_3 (
    .in0(multiplexer_2_out), .in1({{32{1'b0}}, a}), .out(shifted), .sel(comparator_1_eq));
endmodule

module LSL (
  input  [31:0] a,
  input  [31:0] b,
  output [63:0] shifted
);

  wire comparator_1_eq, not_1_out;
  wire [31:0] multiplexer_1_out, subtractor_1_out;
  wire [63:0] multiplexer_2_out, shifter_1_out, shifter_2_out;

  Subtractor #(.width(32)) subtractor_1 (.a(b), .b(32'h1), .out(subtractor_1_out));  // open: bin, bout
  Multiplexer #(.width(32)) multiplexer_1 (.in0(subtractor_1_out), .in1(b), .out(multiplexer_1_out), .sel(b[0]));
  Comparator #(.width(5)) comparator_1 (.a(b[4:0]), .b({5{1'b0}}), .eq(comparator_1_eq));  // open: gt, lt
  Shifter #(.width(64)) shifter_1 (.in({{32{1'b0}}, a}), .\dist ({1'b0, multiplexer_1_out[4:0]}), .out(shifter_1_out));
  not not_1 (not_1_out, b[0]);
  Shifter #(.width(64)) shifter_2 (.in(shifter_1_out), .\dist (6'b000001), .out(shifter_2_out));
  Multiplexer #(.width(64)) multiplexer_2 (
    .in0(shifter_1_out), .in1(shifter_2_out), .out(multiplexer_2_out), .sel(not_1_out));
  Multiplexer #(.width(64)) multiplexer_3 (
    .in0(multiplexer_2_out), .in1({{32{1'b0}}, a}), .out(shifted), .sel(comparator_1_eq));
endmodule

module ASR (
  input  [31:0] a,
  input  [31:0] b,
  output [63:0] shifted
);

  wire comparator_1_lt;
  wire [31:0] multiplexer_1_out, not_1_out;
  wire [63:0] LogicalSR_shifted, not_2_out;

  assign not_1_out = ~a;  // NOT_Gate not_1, 32 bits wide
  Comparator #(.width(32)) comparator_1 (.a(a), .b({32{1'b0}}), .lt(comparator_1_lt));  // open: gt, eq
  Multiplexer #(.width(32)) multiplexer_1 (.in0(a), .in1(not_1_out), .out(multiplexer_1_out), .sel(comparator_1_lt));
  LSR LogicalSR (.a(multiplexer_1_out), .b(b), .shifted(LogicalSR_shifted));
  Multiplexer #(.width(64)) multiplexer_2 (
    .in0(LogicalSR_shifted), .in1(not_2_out), .out(shifted), .sel(comparator_1_lt));
  assign not_2_out = ~LogicalSR_shifted;  // NOT_Gate not_2, 64 bits wide
endmodule

module ROT_R (
  input  [31:0] a,
  input  [31:0] b,
  output [63:0] rotated
);

  wire [31:0] subtractor_1_out;
  wire [63:0] Logical_Shift_Left_shifted, Logical_Shift_Right_shifted, or_1_out;

  Subtractor #(.width(32)) subtractor_1 (.a(32'h20), .b(b), .out(subtractor_1_out));  // open: bin, bout
  LSR Logical_Shift_Right (.a(a), .b(b), .shifted(Logical_Shift_Right_shifted));
  LSL Logical_Shift_Left (.a(a), .b(subtractor_1_out), .shifted(Logical_Shift_Left_shifted));
  assign or_1_out = Logical_Shift_Right_shifted | Logical_Shift_Left_shifted;  // OR_Gate or_1, 64 bits wide
  assign rotated = or_1_out & 64'hffffffff;  // AND_Gate and_1, 64 bits wide
endmodule

module CL_Z (
  input  [31:0] a,
  output [63:0] num_Of_0
);

  wire comparator_1_lt, comparator_2_lt, comparator_3_lt, comparator_4_lt, comparator_5_lt, comparator_6_lt,
       comparator_7_lt, comparator_8_lt, comparator_9_lt, comparator_10_lt, comparator_11_lt,
       comparator_12_lt, comparator_13_lt, comparator_14_lt, comparator_15_lt, comparator_16_lt,
       comparator_17_lt, comparator_18_lt, comparator_19_lt, comparator_20_lt, comparator_21_lt,
       comparator_22_lt, comparator_23_lt, comparator_24_lt, comparator_25_lt, comparator_26_lt,
       comparator_27_lt, comparator_28_lt, comparator_29_lt, comparator_30_lt, comparator_31_lt,
       comparator_32_lt;
  wire [31:0] adder_1_out, adder_2_out, adder_3_out, adder_4_out, adder_5_out, adder_6_out, adder_7_out,
       adder_8_out, adder_9_out, adder_10_out, adder_11_out, adder_12_out, adder_13_out, adder_14_out,
       adder_15_out, adder_16_out, adder_17_out, adder_18_out, adder_19_out, adder_20_out, adder_21_out,
       adder_22_out, adder_23_out, adder_24_out, adder_25_out, adder_26_out, adder_27_out, adder_28_out,
       adder_29_out, adder_30_out, adder_31_out, bit_extender_1_out, bit_extender_2_out, bit_extender_3_out,
       bit_extender_4_out, bit_extender_5_out, bit_extender_6_out, bit_extender_7_out, bit_extender_8_out,
       bit_extender_9_out, bit_extender_10_out, bit_extender_11_out, bit_extender_12_out,
       bit_extender_13_out, bit_extender_14_out, bit_extender_15_out, bit_extender_16_out,
       bit_extender_17_out, bit_extender_18_out, bit_extender_19_out, bit_extender_20_out,
       bit_extender_21_out, bit_extender_22_out, bit_extender_23_out, bit_extender_24_out,
       bit_extender_25_out, bit_extender_26_out, bit_extender_27_out, bit_extender_28_out,
       bit_extender_29_out, bit_extender_30_out, bit_extender_31_out, bit_extender_32_out;
  wire [63:0] t;

  Comparator #(.width(64)) comparator_1 (.a(t), .b(64'h1), .lt(comparator_1_lt));  // open: gt, eq
  Comparator #(.width(64)) comparator_2 (.a(t), .b(64'h2), .lt(comparator_2_lt));  // open: gt, eq
  Comparator #(.width(64)) comparator_3 (.a(t), .b(64'h4), .lt(comparator_3_lt));  // open: gt, eq
  Comparator #(.width(64)) comparator_4 (.a(t), .b(64'h8), .lt(comparator_4_lt));  // open: gt, eq
  Comparator #(.width(64)) comparator_5 (.a(t), .b(64'h10), .lt(comparator_5_lt));  // open: gt, eq
  Comparator #(.width(64)) comparator_6 (.a(t), .b(64'h20), .lt(comparator_6_lt));  // open: gt, eq
  Comparator #(.width(64)) comparator_7 (.a(t), .b(64'h40), .lt(comparator_7_lt));  // open: gt, eq
  Comparator #(.width(64)) comparator_8 (.a(t), .b(64'h80), .lt(comparator_8_lt));  // open: gt, eq
  Comparator #(.width(64)) comparator_9 (.a(t), .b(64'h100), .lt(comparator_9_lt));  // open: gt, eq
  Comparator #(.width(64)) comparator_10 (.a(t), .b(64'h200), .lt(comparator_10_lt));  // open: gt, eq
  Comparator #(.width(64)) comparator_11 (.a(t), .b(64'h400), .lt(comparator_11_lt));  // open: gt, eq
  Comparator #(.width(64)) comparator_12 (.a(t), .b(64'h800), .lt(comparator_12_lt));  // open: gt, eq
  Comparator #(.width(64)) comparator_13 (.a(t), .b(64'h1000), .lt(comparator_13_lt));  // open: gt, eq
  Comparator #(.width(64)) comparator_14 (.a(t), .b(64'h2000), .lt(comparator_14_lt));  // open: gt, eq
  Comparator #(.width(64)) comparator_15 (.a(t), .b(64'h4000), .lt(comparator_15_lt));  // open: gt, eq
  Comparator #(.width(64)) comparator_16 (.a(t), .b(64'h8000), .lt(comparator_16_lt));  // open: gt, eq
  Comparator #(.width(64)) comparator_17 (.a(t), .b(64'h10000), .lt(comparator_17_lt));  // open: gt, eq
  Comparator #(.width(64)) comparator_18 (.a(t), .b(64'h20000), .lt(comparator_18_lt));  // open: gt, eq
  Comparator #(.width(64)) comparator_19 (.a(t), .b(64'h40000), .lt(comparator_19_lt));  // open: gt, eq
  Comparator #(.width(64)) comparator_20 (.a(t), .b(64'h80000), .lt(comparator_20_lt));  // open: gt, eq
  Comparator #(.width(64)) comparator_21 (.a(t), .b(64'h100000), .lt(comparator_21_lt));  // open: gt, eq
  Comparator #(.width(64)) comparator_22 (.a(t), .b(64'h200000), .lt(comparator_22_lt));  // open: gt, eq
  Comparator #(.width(64)) comparator_23 (.a(t), .b(64'h400000), .lt(comparator_23_lt));  // open: gt, eq
  Comparator #(.width(64)) comparator_24 (.a(t), .b(64'h800000), .lt(comparator_24_lt));  // open: gt, eq
  Comparator #(.width(64)) comparator_25 (.a(t), .b(64'h1000000), .lt(comparator_25_lt));  // open: gt, eq
  Comparator #(.width(64)) comparator_26 (.a(t), .b(64'h2000000), .lt(comparator_26_lt));  // open: gt, eq
  Comparator #(.width(64)) comparator_27 (.a(t), .b(64'h4000000), .lt(comparator_27_lt));  // open: gt, eq
  Comparator #(.width(64)) comparator_28 (.a(t), .b(64'h8000000), .lt(comparator_28_lt));  // open: gt, eq
  Comparator #(.width(64)) comparator_29 (.a(t), .b(64'h10000000), .lt(comparator_29_lt));  // open: gt, eq
  Comparator #(.width(64)) comparator_30 (.a(t), .b(64'h20000000), .lt(comparator_30_lt));  // open: gt, eq
  Comparator #(.width(64)) comparator_31 (.a(t), .b(64'h40000000), .lt(comparator_31_lt));  // open: gt, eq
  Comparator #(.width(64)) comparator_32 (.a(t), .b(64'h80000000), .lt(comparator_32_lt));  // open: gt, eq
  assign bit_extender_1_out = {{31{1'b0}}, comparator_1_lt};  // Bit_Extender bit_extender_1
  assign bit_extender_2_out = {{31{1'b0}}, comparator_2_lt};  // Bit_Extender bit_extender_2
  assign bit_extender_3_out = {{31{1'b0}}, comparator_3_lt};  // Bit_Extender bit_extender_3
  assign bit_extender_4_out = {{31{1'b0}}, comparator_4_lt};  // Bit_Extender bit_extender_4
  assign bit_extender_5_out = {{31{1'b0}}, comparator_5_lt};  // Bit_Extender bit_extender_5
  assign bit_extender_6_out = {{31{1'b0}}, comparator_6_lt};  // Bit_Extender bit_extender_6
  assign bit_extender_7_out = {{31{1'b0}}, comparator_7_lt};  // Bit_Extender bit_extender_7
  assign bit_extender_8_out = {{31{1'b0}}, comparator_8_lt};  // Bit_Extender bit_extender_8
  assign bit_extender_9_out = {{31{1'b0}}, comparator_9_lt};  // Bit_Extender bit_extender_9
  assign bit_extender_10_out = {{31{1'b0}}, comparator_10_lt};  // Bit_Extender bit_extender_10
  assign bit_extender_11_out = {{31{1'b0}}, comparator_11_lt};  // Bit_Extender bit_extender_11
  assign bit_extender_12_out = {{31{1'b0}}, comparator_12_lt};  // Bit_Extender bit_extender_12
  assign bit_extender_13_out = {{31{1'b0}}, comparator_13_lt};  // Bit_Extender bit_extender_13
  assign bit_extender_14_out = {{31{1'b0}}, comparator_14_lt};  // Bit_Extender bit_extender_14
  assign bit_extender_15_out = {{31{1'b0}}, comparator_15_lt};  // Bit_Extender bit_extender_15
  assign bit_extender_16_out = {{31{1'b0}}, comparator_16_lt};  // Bit_Extender bit_extender_16
  assign bit_extender_17_out = {{31{1'b0}}, comparator_17_lt};  // Bit_Extender bit_extender_17
  assign bit_extender_18_out = {{31{1'b0}}, comparator_18_lt};  // Bit_Extender bit_extender_18
  assign bit_extender_19_out = {{31{1'b0}}, comparator_19_lt};  // Bit_Extender bit_extender_19
  assign bit_extender_20_out = {{31{1'b0}}, comparator_20_lt};  // Bit_Extender bit_extender_20
  assign bit_extender_21_out = {{31{1'b0}}, comparator_21_lt};  // Bit_Extender bit_extender_21
  assign bit_extender_22_out = {{31{1'b0}}, comparator_22_lt};  // Bit_Extender bit_extender_22
  assign bit_extender_23_out = {{31{1'b0}}, comparator_23_lt};  // Bit_Extender bit_extender_23
  assign bit_extender_24_out = {{31{1'b0}}, comparator_24_lt};  // Bit_Extender bit_extender_24
  assign bit_extender_25_out = {{31{1'b0}}, comparator_25_lt};  // Bit_Extender bit_extender_25
  assign bit_extender_26_out = {{31{1'b0}}, comparator_26_lt};  // Bit_Extender bit_extender_26
  assign bit_extender_27_out = {{31{1'b0}}, comparator_27_lt};  // Bit_Extender bit_extender_27
  assign bit_extender_28_out = {{31{1'b0}}, comparator_28_lt};  // Bit_Extender bit_extender_28
  assign bit_extender_29_out = {{31{1'b0}}, comparator_29_lt};  // Bit_Extender bit_extender_29
  assign bit_extender_30_out = {{31{1'b0}}, comparator_30_lt};  // Bit_Extender bit_extender_30
  assign bit_extender_31_out = {{31{1'b0}}, comparator_31_lt};  // Bit_Extender bit_extender_31
  assign bit_extender_32_out = {{31{1'b0}}, comparator_32_lt};  // Bit_Extender bit_extender_32
  Adder #(.width(32)) adder_1 (.a(bit_extender_1_out), .b(bit_extender_2_out), .out(adder_1_out));  // open: cin, cout
  Adder #(.width(32)) adder_2 (.a(adder_1_out), .b(bit_extender_3_out), .out(adder_2_out));  // open: cin, cout
  Adder #(.width(32)) adder_3 (.a(adder_2_out), .b(bit_extender_4_out), .out(adder_3_out));  // open: cin, cout
  Adder #(.width(32)) adder_4 (.a(adder_3_out), .b(bit_extender_5_out), .out(adder_4_out));  // open: cin, cout
  Adder #(.width(32)) adder_5 (.a(adder_4_out), .b(bit_extender_6_out), .out(adder_5_out));  // open: cin, cout
  Adder #(.width(32)) adder_6 (.a(adder_5_out), .b(bit_extender_7_out), .out(adder_6_out));  // open: cin, cout
  Adder #(.width(32)) adder_7 (.a(adder_6_out), .b(bit_extender_8_out), .out(adder_7_out));  // open: cin, cout
  Adder #(.width(32)) adder_8 (.a(adder_7_out), .b(bit_extender_9_out), .out(adder_8_out));  // open: cin, cout
  Adder #(.width(32)) adder_9 (.a(adder_8_out), .b(bit_extender_10_out), .out(adder_9_out));  // open: cin, cout
  Adder #(.width(32)) adder_10 (.a(adder_9_out), .b(bit_extender_11_out), .out(adder_10_out));  // open: cin, cout
  Adder #(.width(32)) adder_11 (.a(adder_10_out), .b(bit_extender_12_out), .out(adder_11_out));  // open: cin, cout
  Adder #(.width(32)) adder_12 (.a(adder_11_out), .b(bit_extender_13_out), .out(adder_12_out));  // open: cin, cout
  Adder #(.width(32)) adder_13 (.a(adder_12_out), .b(bit_extender_14_out), .out(adder_13_out));  // open: cin, cout
  Adder #(.width(32)) adder_14 (.a(adder_13_out), .b(bit_extender_15_out), .out(adder_14_out));  // open: cin, cout
  Adder #(.width(32)) adder_15 (.a(adder_14_out), .b(bit_extender_16_out), .out(adder_15_out));  // open: cin, cout
  Adder #(.width(32)) adder_16 (.a(adder_15_out), .b(bit_extender_17_out), .out(adder_16_out));  // open: cin, cout
  Adder #(.width(32)) adder_17 (.a(adder_16_out), .b(bit_extender_18_out), .out(adder_17_out));  // open: cin, cout
  Adder #(.width(32)) adder_18 (.a(adder_17_out), .b(bit_extender_19_out), .out(adder_18_out));  // open: cin, cout
  Adder #(.width(32)) adder_19 (.a(adder_18_out), .b(bit_extender_20_out), .out(adder_19_out));  // open: cin, cout
  Adder #(.width(32)) adder_20 (.a(adder_19_out), .b(bit_extender_21_out), .out(adder_20_out));  // open: cin, cout
  Adder #(.width(32)) adder_21 (.a(adder_20_out), .b(bit_extender_22_out), .out(adder_21_out));  // open: cin, cout
  Adder #(.width(32)) adder_22 (.a(adder_21_out), .b(bit_extender_23_out), .out(adder_22_out));  // open: cin, cout
  Adder #(.width(32)) adder_23 (.a(adder_22_out), .b(bit_extender_24_out), .out(adder_23_out));  // open: cin, cout
  Adder #(.width(32)) adder_24 (.a(adder_23_out), .b(bit_extender_25_out), .out(adder_24_out));  // open: cin, cout
  Adder #(.width(32)) adder_25 (.a(adder_24_out), .b(bit_extender_26_out), .out(adder_25_out));  // open: cin, cout
  Adder #(.width(32)) adder_26 (.a(adder_25_out), .b(bit_extender_27_out), .out(adder_26_out));  // open: cin, cout
  Adder #(.width(32)) adder_27 (.a(adder_26_out), .b(bit_extender_28_out), .out(adder_27_out));  // open: cin, cout
  Adder #(.width(32)) adder_28 (.a(adder_27_out), .b(bit_extender_29_out), .out(adder_28_out));  // open: cin, cout
  Adder #(.width(32)) adder_29 (.a(adder_28_out), .b(bit_extender_30_out), .out(adder_29_out));  // open: cin, cout
  Adder #(.width(32)) adder_30 (.a(adder_29_out), .b(bit_extender_31_out), .out(adder_30_out));  // open: cin, cout
  Adder #(.width(32)) adder_31 (.a(adder_30_out), .b(bit_extender_32_out), .out(adder_31_out));  // open: cin, cout
  assign num_Of_0 = {{32{1'b0}}, adder_31_out};  // Bit_Extender bit_extender_33
  assign t = {{32{1'b0}}, a};  // Bit_Extender bit_extender_34
endmodule

module CL_O (
  input  [31:0] a,
  output [63:0] num_Of_1
);

  wire [31:0] not_1_out;

  assign not_1_out = ~a;  // NOT_Gate not_1, 32 bits wide
  CL_Z CLZ (.a(not_1_out), .num_Of_0(num_Of_1));
endmodule

module ALU_CONTROL (
  input  [5:0] op,
  input  [5:0] func,
  input  exe,
  output [3:0] aluOp
);

  wire comparator_1_eq, comparator_2_eq, comparator_3_eq, not_2_out, or_1_out, os, s;
  wire [3:0] multiplexer_1_out, multiplexer_2_out, multiplexer_3_out, multiplexer_4_out;

  xor xor_1 (os, op[0], op[1]);
  Comparator #(.width(6)) comparator_1 (.a(op), .b({6{1'b0}}), .eq(comparator_1_eq));  // open: gt, lt
  not not_1 (s, comparator_1_eq);
  Comparator #(.width(6)) comparator_2 (.a(op), .b(6'b000100), .eq(comparator_2_eq));  // open: gt, lt
  Multiplexer #(.select(4), .width(4)) multiplexer_1 (
    .in0(4'b1001), .in2(4'b0011), .in4(4'b1001), .in6(4'b1010), .in7(4'b1011), .in8(4'b0000), .in10(4'b0001),
    .in12(4'b0100), .in13(4'b0101), .in14(4'b0110), .out(multiplexer_1_out), .sel({func[5], func[2:0]}));  // open: in1, in3, in5, in9, in11, in15
  or or_1 (or_1_out, os, comparator_2_eq);
  Multiplexer #(.width(4)) multiplexer_2 (.in0(4'b0000), .in1(4'b0001), .out(multiplexer_2_out), .sel(or_1_out));
  Multiplexer #(.width(4)) multiplexer_3 (
    .in0(multiplexer_2_out), .in1(4'b0010), .out(multiplexer_3_out), .sel(comparator_3_eq));
  Multiplexer #(.width(4)) multiplexer_4 (
    .in0(multiplexer_1_out), .in1(multiplexer_3_out), .out(multiplexer_4_out), .sel(s));
  Comparator #(.width(6)) comparator_3 (.a(op), .b(6'b011100), .eq(comparator_3_eq));  // open: gt, lt
  Multiplexer #(.width(4)) multiplexer_5 (.in0(multiplexer_4_out), .in1(4'b0000), .out(aluOp), .sel(not_2_out));
  not not_2 (not_2_out, exe);

  // Other names for the same wires on the sheet: slct[3:0] = {func[5], func[2:0]}
endmodule

module CONTROL (
  input  [5:0] opcode,
  input  [5:0] func,
  input  exe,
  output [3:0] aluOp,
  output mem_to_reg,
  output RegDst,
  output MemWrite,
  output RegWrite,
  output Div,
  output BranchNEQ,
  output Jump,
  output ALUSrc,
  output sll_s,
  output slti,
  output mf,
  output hi,
  output mul,
  output BranchEQ,
  output jr,
  output jal
);

  wire comparator_1_eq, comparator_3_eq, comparator_5_eq, comparator_8_eq, comparator_9_eq, comparator_10_eq,
       comparator_12_eq, comparator_13_eq, comparator_14_eq, comparator_16_eq, comparator_18_eq, not_1_out,
       not_2_out, not_3_out, not_4_out, or_1_out, or_2_out;

  Comparator #(.width(6)) comparator_1 (.a(func), .b(6'b000010), .eq(comparator_1_eq));  // open: gt, lt
  Comparator #(.width(6)) comparator_2 (.a(6'b100011), .b(opcode), .eq(mem_to_reg));  // open: gt, lt
  Comparator #(.width(6)) comparator_3 (.a({6{1'b0}}), .b(opcode), .eq(comparator_3_eq));  // open: gt, lt
  Comparator #(.width(6)) comparator_4 (.a(6'b101011), .b(opcode), .eq(MemWrite));  // open: gt, lt
  Comparator #(.width(6)) comparator_5 (.a(func), .b(6'b011010), .eq(comparator_5_eq));  // open: gt, lt
  Comparator #(.width(6)) comparator_6 (.a(6'b000101), .b(opcode), .eq(BranchNEQ));  // open: gt, lt
  Comparator #(.width(6)) comparator_7 (.a(6'b000010), .b(opcode), .eq(Jump));  // open: gt, lt
  Comparator #(.width(6)) comparator_8 (.a({6{1'b0}}), .b(opcode), .eq(comparator_8_eq));  // open: gt, lt
  Comparator #(.width(6)) comparator_9 (.a(opcode), .b(6'b000101), .eq(comparator_9_eq));  // open: gt, lt
  Comparator #(.width(6)) comparator_10 (.a(func), .b({6{1'b0}}), .eq(comparator_10_eq));  // open: gt, lt
  Comparator #(.width(6)) comparator_11 (.a(6'b001010), .b(opcode), .eq(slti));  // open: gt, lt
  Comparator #(.width(6)) comparator_12 (.a(6'b010000), .b(func), .eq(comparator_12_eq));  // open: gt, lt
  Comparator #(.width(6)) comparator_13 (.a(6'b010010), .b(func), .eq(comparator_13_eq));  // open: gt, lt
  Comparator #(.width(6)) comparator_14 (.a(6'b011100), .b(opcode), .eq(comparator_14_eq));  // open: gt, lt
  Comparator #(.width(6)) comparator_15 (.a(opcode), .b(6'b000100), .eq(BranchEQ));  // open: gt, lt
  Comparator #(.width(6)) comparator_16 (.a(func), .b(6'b001000), .eq(comparator_16_eq));  // open: gt, lt
  Comparator #(.width(6)) comparator_17 (.a(opcode), .b(6'b000011), .eq(jal));  // open: gt, lt
  not not_1 (not_1_out, comparator_3_eq);
  not not_2 (not_2_out, comparator_8_eq);
  not not_3 (not_3_out, comparator_9_eq);
  ALU_CONTROL Control_ALU (.op(opcode), .func(func), .exe(exe), .aluOp(aluOp));
  Comparator #(.width(6)) comparator_18 (.a(opcode), .b({6{1'b0}}), .eq(comparator_18_eq));  // open: gt, lt
  and and_1 (mul, comparator_1_eq, comparator_14_eq);
  or or_1 (or_1_out, not_1_out, mul);
  and and_2 (Div, comparator_3_eq, comparator_5_eq);
  or or_2 (or_2_out, comparator_12_eq, comparator_13_eq);
  and and_3 (jr, comparator_16_eq, comparator_18_eq);
  and and_4 (sll_s, comparator_3_eq, comparator_10_eq);
  not not_4 (not_4_out, mul);
  and and_5 (RegDst, or_1_out, not_4_out);
  and and_6 (mf, comparator_3_eq, or_2_out);
  and and_7 (ALUSrc, not_2_out, not_4_out, not_3_out);
  nor nor_1 (RegWrite, BranchEQ, MemWrite, Div, BranchNEQ, Jump, jr);
  and and_8 (hi, mf, comparator_12_eq);
endmodule

module counter5 (
  input  en,
  input  clk,
  input  reset,
  output [2:0] num
);

  wire comparator_1_gt;
  wire [2:0] adder_1_out, multiplexer_1_out;

  Adder #(.width(3)) adder_1 (.a(num), .b(3'b001), .out(adder_1_out));  // open: cin, cout
  Multiplexer #(.width(3)) multiplexer_1 (
    .in0(adder_1_out), .in1(3'b000), .out(multiplexer_1_out), .sel(comparator_1_gt));
  Comparator #(.mode("unsigned"), .width(3)) comparator_1 (
    .a(adder_1_out), .b(3'b100), .gt(comparator_1_gt));  // open: eq, lt
  Register #(.width(3)) register_1 (.D(multiplexer_1_out), .en(en), .clk(clk), .Q(num), .clr(reset));
endmodule

module State_Finder (
  input  halt,
  input  clk,
  input  reset,
  output instruction_fetch,
  output instruction_decode,
  output exec,
  output mem,
  output wb
);

  wire not_1_out;
  wire [2:0] counter_num;

  not not_1 (not_1_out, halt);
  counter5 counter (.en(not_1_out), .clk(clk), .reset(reset), .num(counter_num));
  Comparator #(.mode("unsigned"), .width(3)) comparator_1 (
    .a(counter_num), .b(3'b000), .eq(instruction_fetch));  // open: gt, lt
  Comparator #(.mode("unsigned"), .width(3)) comparator_2 (
    .a(counter_num), .b(3'b001), .eq(instruction_decode));  // open: gt, lt
  Comparator #(.mode("unsigned"), .width(3)) comparator_3 (.a(counter_num), .b(3'b010), .eq(exec));  // open: gt, lt
  Comparator #(.mode("unsigned"), .width(3)) comparator_4 (.a(counter_num), .b(3'b011), .eq(mem));  // open: gt, lt
  Comparator #(.mode("unsigned"), .width(3)) comparator_5 (.a(counter_num), .b(3'b100), .eq(wb));  // open: gt, lt
endmodule
