// Logisim project third.circ as structural Verilog: 13 circuits, main circuit main
module main (
  input  [31:0] a,
  input  [31:0] b,
  input  [3:0] aluop,
  input  output_inverted,
  input  output_inc,
  input  clk,
  input  rst,
  output [31:0] res_low,
  output done,
  output [31:0] res_high
);

  wire adder_2_cout, comparator_1_eq, comparator_2_eq, comparator_3_eq, comparator_4_eq, comparator_5_eq,
       done_DIV, done_MULT, not_2_out, not_3_out, not_4_out, or_1_out, or_2_out, start, SUB_cout;
  wire [0:0] ADD_HIGH;
  wire [3:0] aluop_Reg_q;
  wire [31:0] a_Reg_q, ADD_LOW, adder_1_out, adder_2_out, AND_LOW, ASR_HIGH, ASR_LOW, b_Reg_q, CLO_HIGH,
       CLO_LOW, CLZ_HIGH, CLZ_LOW, DIV_HIGH, DIV_LOW, LSL_HIGH, LSL_LOW, LSR_HIGH, LSR_LOW, MUL_HIGH,
       MUL_LOW, multiplexer_2_out, multiplexer_3_out, multiplexer_4_out, multiplexer_5_out, not_1_out,
       not_5_out, not_6_out, OR_LOW, ROTR_HIGH, ROTR_LOW, SUB_HIGH, SUB_LOW, undriven, undriven_2,
       undriven_3, undriven_4, undriven_5, undriven_6, XOR_LOW;

  assign not_1_out = ~b;  // NOT_Gate not_1, 32 bits wide
  Register #(.width(32)) a_Reg (.D(a), .clk(clk), .Q(a_Reg_q));  // open: en, clr
  Register #(.width(32)) b_Reg (.D(b), .clk(clk), .Q(b_Reg_q));  // open: en, clr
  Register #(.width(4)) aluop_Reg (.D(aluop), .clk(clk), .Q(aluop_Reg_q));  // open: en, clr
  CSA Sum (.a(a), .b(b), .s(ADD_LOW), .cout(ADD_HIGH[0]));  // open: cin
  CSA SUB (.cin(1'b1), .a(a), .b(not_1_out), .s(SUB_LOW), .cout(SUB_cout));
  not not_2 (not_2_out, comparator_1_eq);
  Comparator #(.width(32)) comparator_1 (.a(a_Reg_q), .b(a), .eq(comparator_1_eq));  // open: gt, lt
  not not_3 (not_3_out, comparator_2_eq);
  Comparator #(.width(32)) comparator_2 (.a(b_Reg_q), .b(b), .eq(comparator_2_eq));  // open: gt, lt
  not not_4 (not_4_out, comparator_3_eq);
  Comparator #(.width(4)) comparator_3 (.a(aluop_Reg_q), .b(aluop), .eq(comparator_3_eq));  // open: gt, lt
  Multiplexer #(.width(32)) multiplexer_1 (.in0({32{1'b1}}), .in1({32{1'b0}}), .out(SUB_HIGH), .sel(SUB_cout));
  LSR Logical_Shift_Right (.a(a), .b(b), .shifted({LSR_HIGH, LSR_LOW}));
  LSL Logical_Shift_Left (.a(a), .b(b), .shifted({LSL_HIGH, LSL_LOW}));
  CL_O cl_o_1 (.in_1(a), .num_Of_1({CLO_HIGH, CLO_LOW}));
  or or_1 (or_1_out, not_2_out, not_4_out, not_3_out);
  Comparator #(.width(4)) comparator_4 (.a(aluop), .b(4'b0010), .eq(comparator_4_eq));  // open: gt, lt
  Comparator #(.width(4)) comparator_5 (.a(aluop), .b(4'b0011), .eq(comparator_5_eq));  // open: gt, lt
  or or_2 (or_2_out, comparator_4_eq, comparator_5_eq);
  Multiplexer #(.select(4), .width(32)) multiplexer_2 (
    .in0(ADD_LOW), .in1(SUB_LOW), .in2(MUL_LOW), .in3(DIV_LOW), .in4(AND_LOW), .in5(OR_LOW), .in6(XOR_LOW),
    .in7(CLO_LOW), .in8(CLZ_LOW), .in9(LSL_LOW), .in10(LSR_LOW), .in11(ASR_LOW), .in12(ROTR_LOW),
    .in13(undriven_4), .in14(undriven_5), .in15(undriven_6), .out(multiplexer_2_out), .sel(aluop));
  Multiplexer #(.select(4), .width(32)) multiplexer_3 (
    .in0({{31{1'b0}}, ADD_HIGH[0]}), .in1(SUB_HIGH), .in2(MUL_HIGH), .in3(DIV_HIGH), .in4({32{1'b0}}),
    .in5({32{1'b0}}), .in6({32{1'b0}}), .in7(CLO_HIGH), .in8(CLZ_HIGH), .in9(LSL_HIGH), .in10(LSR_HIGH),
    .in11(ASR_HIGH), .in12(ROTR_HIGH), .in13(undriven), .in14(undriven_2), .in15(undriven_3),
    .out(multiplexer_3_out), .sel(aluop));
  and and_1 (start, or_1_out, or_2_out);
  assign not_5_out = ~multiplexer_2_out;  // NOT_Gate not_5, 32 bits wide
  Multiplexer #(.width(32)) multiplexer_4 (
    .in0(multiplexer_3_out), .in1(not_6_out), .out(multiplexer_4_out), .sel(output_inverted));
  assign not_6_out = ~multiplexer_3_out;  // NOT_Gate not_6, 32 bits wide
  Multiplexer #(.width(32)) multiplexer_5 (
    .in0(multiplexer_2_out), .in1(not_5_out), .out(multiplexer_5_out), .sel(output_inverted));
  Adder #(.width(32)) adder_1 (
    .a(multiplexer_4_out), .b({32{1'b0}}), .out(adder_1_out), .cin(adder_2_cout));  // open: cout
  mul Multiplier (.clk(clk), .start(start), .a(a), .b(b), .done(done_MULT), .Result({MUL_HIGH, MUL_LOW}));
  Div Divider (
    .start(start), .clk(clk), .dividend(a), .divisor(b), .done(done_DIV), .remainder(DIV_HIGH),
    .quotient(DIV_LOW));
  ASR Arithmetic_Shift_Right (.a(a), .b(b), .shifted({ASR_HIGH, ASR_LOW}));
  ROT_R Rotate_Right (.a(a), .b(b), .rotated({ROTR_HIGH, ROTR_LOW}));
  CL_Z cl_z_1 (.a(a), .num_Of_0({CLZ_HIGH, CLZ_LOW}));
  Adder #(.width(32)) adder_2 (.a(multiplexer_5_out), .b(32'h1), .out(adder_2_out), .cout(adder_2_cout));  // open: cin
  Multiplexer #(.width(32)) multiplexer_6 (
    .in0(multiplexer_4_out), .in1(adder_1_out), .out(res_high), .sel(output_inc));
  Multiplexer #(.width(32)) multiplexer_7 (.in0(multiplexer_5_out), .in1(adder_2_out), .out(res_low), .sel(output_inc));
  assign AND_LOW = a & b;  // AND_Gate and_2, 32 bits wide
  assign OR_LOW = a | b;  // OR_Gate or_3, 32 bits wide
  assign XOR_LOW = a ^ b;  // XOR_Gate xor_1, 32 bits wide
  Multiplexer #(.select(4)) multiplexer_8 (
    .in0(1'b1), .in1(1'b1), .in2(done_MULT), .in3(done_DIV), .in4(1'b1), .in5(1'b1), .in6(1'b1), .in7(1'b1),
    .in8(1'b1), .in9(1'b1), .in10(1'b1), .in11(1'b1), .in12(1'b1), .in13(1'b1), .in14(1'b1), .in15(1'b1),
    .out(done), .sel(aluop));

  // Other names for the same wires on the sheet: inc = output_inc; invert = output_inverted

  // Notes on the sheet:
  //   a: initial=0x9fb0d13f
endmodule

module counter2 (
  input  clk,
  input  reset,
  output num
);

  wire adder_1_out;

  Adder #(.width(1)) adder_1 (.a(num), .b(1'b1), .out(adder_1_out));  // open: cin, cout
  Register #(.width(1)) register_1 (.D(adder_1_out), .clk(clk), .Q(num), .clr(reset));  // open: en
endmodule

module Div (
  input  start,
  input  clk,
  input  [31:0] dividend,
  input  [31:0] divisor,
  output done,
  output [31:0] remainder,
  output [31:0] quotient
);

  wire comparator_1_gt, comparator_2_lt, counter_div_num, not_1_out, not_3_out, undriven;
  wire [7:0] adder_1_out, counter_q;
  wire [31:0] adder_2_out, multiplexer_1_out, multiplexer_2_out, multiplexer_3_out, multiplexer_4_out,
       multiplexer_5_out, shifter_1_out, shifter_1_out_2, subtractor_1_out;
  wire [63:0] q_q;

  not not_1 (not_1_out, counter_div_num);
  Multiplexer #(.width(32)) multiplexer_1 (
    .in0(q_q[31:0]), .in1(adder_2_out), .out(multiplexer_1_out), .sel(not_3_out));
  Adder adder_1 (.a(counter_q), .b(8'h1), .out(adder_1_out));  // open: cin, cout
  Register counter (.D(adder_1_out), .en(not_1_out), .clk(clk), .Q(counter_q), .clr(start));
  Multiplexer #(.width(32)) multiplexer_2 (
    .in0(shifter_1_out_2), .in1(multiplexer_3_out), .out(multiplexer_2_out), .sel(counter_div_num));
  Multiplexer #(.width(32)) multiplexer_3 (
    .in0(q_q[63:32]), .in1(subtractor_1_out), .out(multiplexer_3_out), .sel(not_3_out));
  Multiplexer #(.width(32)) multiplexer_4 (
    .in0(shifter_1_out), .in1(multiplexer_1_out), .out(multiplexer_4_out), .sel(counter_div_num));
  Multiplexer #(.width(32)) multiplexer_5 (
    .in0(multiplexer_4_out), .in1(dividend), .out(multiplexer_5_out), .sel(start));
  Register #(.width(32)) a (.D(multiplexer_2_out), .en(done), .clk(clk), .Q(q_q[63:32]), .clr(start));
  Register #(.width(32)) q (.D(multiplexer_5_out), .en(done), .clk(clk), .Q(q_q[31:0]), .clr(undriven));
  counter2 counter_div (.clk(clk), .reset(start), .num(counter_div_num));
  Comparator comparator_1 (.a(counter_q), .b(8'h20), .gt(comparator_1_gt));  // open: eq, lt
  Comparator #(.mode("unsigned"), .width(32)) comparator_2 (
    .a(q_q[63:32]), .b(divisor), .lt(comparator_2_lt));  // open: gt, eq
  not not_2 (done, comparator_1_gt);
  Shifter #(.width(64)) shifter_1 (.in(q_q), .\dist (6'b000001), .out({shifter_1_out_2, shifter_1_out}));
  not not_3 (not_3_out, comparator_2_lt);
  Register #(.width(32)) register_1 (.D(q_q[63:32]), .en(done), .clk(clk), .Q(remainder));  // open: clr
  Subtractor #(.width(32)) subtractor_1 (.a(q_q[63:32]), .b(divisor), .out(subtractor_1_out));  // open: bin, bout
  Adder #(.width(32)) adder_2 (.a(q_q[31:0]), .b(32'h1), .out(adder_2_out));  // open: cin, cout
  Register #(.width(32)) register_2 (.D(q_q[31:0]), .en(done), .clk(clk), .Q(quotient));  // open: clr
endmodule

module CSA (
  input  cin,
  input  [31:0] a,
  input  [31:0] b,
  output [31:0] s,
  output cout
);

  wire adder_1_cout, adder_2_cout, adder_3_cout, adder_4_cout, adder_5_cout, adder_6_cout, adder_7_cout,
       multiplexer_2_out, multiplexer_3_out;
  wire [7:0] adder_2_out, adder_3_out, adder_4_out, adder_5_out, adder_6_out, adder_7_out;

  Adder adder_1 (.a(a[7:0]), .b(b[7:0]), .out(s[7:0]), .cin(cin), .cout(adder_1_cout));
  Adder adder_2 (.a(a[15:8]), .b(b[15:8]), .out(adder_2_out), .cout(adder_2_cout));  // open: cin
  Adder adder_3 (.a(a[15:8]), .b(b[15:8]), .out(adder_3_out), .cin(1'b1), .cout(adder_3_cout));
  Adder adder_4 (.a(a[23:16]), .b(b[23:16]), .out(adder_4_out), .cout(adder_4_cout));  // open: cin
  Adder adder_5 (.a(a[23:16]), .b(b[23:16]), .out(adder_5_out), .cin(1'b1), .cout(adder_5_cout));
  Adder adder_6 (.a(a[31:24]), .b(b[31:24]), .out(adder_6_out), .cout(adder_6_cout));  // open: cin
  Adder adder_7 (.a(a[31:24]), .b(b[31:24]), .out(adder_7_out), .cin(1'b1), .cout(adder_7_cout));
  Multiplexer #(.width(8)) multiplexer_1 (.in0(adder_2_out), .in1(adder_3_out), .out(s[15:8]), .sel(adder_1_cout));
  Multiplexer multiplexer_2 (.in0(adder_2_cout), .in1(adder_3_cout), .out(multiplexer_2_out), .sel(adder_1_cout));
  Multiplexer multiplexer_3 (.in0(adder_4_cout), .in1(adder_5_cout), .out(multiplexer_3_out), .sel(multiplexer_2_out));
  Multiplexer #(.width(8)) multiplexer_4 (
    .in0(adder_6_out), .in1(adder_7_out), .out(s[31:24]), .sel(multiplexer_3_out));
  Multiplexer multiplexer_5 (.in0(adder_6_cout), .in1(adder_7_cout), .out(cout), .sel(multiplexer_3_out));
  Multiplexer #(.width(8)) multiplexer_6 (
    .in0(adder_4_out), .in1(adder_5_out), .out(s[23:16]), .sel(multiplexer_2_out));
endmodule

module CsaveA (
  input  cin,
  input  [31:0] a,
  input  [31:0] b,
  input  [31:0] c,
  output [31:0] s,
  output COUT2,
  output COUT1,
  output COUT0
);

  wire CSAAdder_cout;
  wire [31:0] adders_cout, adders_s, shifter_1_out;

  Parallel_FullAdders adders (.a(a), .b(b), .cin(c), .s(adders_s), .cout(adders_cout));
  Shifter #(.width(32)) shifter_1 (.in(adders_cout), .\dist (5'b00001), .out(shifter_1_out));
  CSA CSAAdder (.cin(cin), .a(adders_s), .b(shifter_1_out), .s(s), .cout(CSAAdder_cout));
  and and_1 (COUT2, CSAAdder_cout, adders_cout[31]);
  xor xor_1 (COUT1, CSAAdder_cout, adders_cout[31]);
  nor nor_1 (COUT0, CSAAdder_cout, adders_cout[31]);
endmodule

module Parallel_FullAdders (
  input  [31:0] a,
  input  [31:0] b,
  input  [31:0] cin,
  output [31:0] s,
  output [31:0] cout
);

  wire [31:0] and_1_out, and_2_out, xor_1_out;

  assign and_1_out = a & b;  // AND_Gate and_1, 32 bits wide
  assign xor_1_out = a ^ b;  // XOR_Gate xor_1, 32 bits wide
  assign and_2_out = xor_1_out & cin;  // AND_Gate and_2, 32 bits wide
  assign s = xor_1_out ^ cin;  // XOR_Gate xor_2, 32 bits wide
  assign cout = and_2_out | and_1_out;  // OR_Gate or_1, 32 bits wide
endmodule

module mul (
  input  clk,
  input  start,
  input  [31:0] a,
  input  [31:0] b,
  output done,
  output [63:0] Result
);

  wire and_1_out, comparator_1_gt, comparator_1_lt, CSA_cout1, CSA_cout2, Init, nor_1_out, not_1_out,
       not_2_out, not_3_out, Opperation, or_1_out, or_2_out, or_3_out, or_4_out, or_5_out, OR_R1_FLAG, RE_q,
       RE_signal, signal_1, signal_2, undriven;
  wire [31:0] adder_1_out, CSA2_s, CSA_s, multiplexer_1_out, multiplexer_2_out, multiplexer_3_out,
       multiplexer_4_out, multiplexer_5_out, multiplexer_6_out, R1_q, R2_q, R2_q_2, shifter_1_out,
       shifter_3_out;
  wire [63:0] multiplexer_7_out, multiplexer_8_out, shifter_2_out, shifter_4_out;

  not not_1 (not_1_out, OR_R1_FLAG);
  Multiplexer #(.width(32)) multiplexer_1 (
    .in0({32{1'b0}}), .in1(shifter_2_out[31:0]), .out(multiplexer_1_out), .sel(shifter_1_out[0]));
  Multiplexer #(.width(32)) multiplexer_2 (.in0({32{1'b0}}), .in1(R2_q_2), .out(multiplexer_2_out), .sel(R1_q[0]));
  Multiplexer #(.width(32)) multiplexer_3 (
    .in0({32{1'b0}}), .in1(shifter_2_out[63:32]), .out(multiplexer_3_out), .sel(shifter_1_out[0]));
  nor nor_1 (nor_1_out, Opperation, start);
  and and_1 (and_1_out, not_1_out, Opperation);
  Multiplexer #(.width(32)) multiplexer_4 (.in0({32{1'b0}}), .in1(R2_q), .out(multiplexer_4_out), .sel(R1_q[0]));
  and and_2 (signal_1, Init, start);
  Shifter #(.shift("lr"), .width(32)) shifter_1 (.in(R1_q), .\dist (5'b00001), .out(shifter_1_out));
  or or_1 (or_1_out, nor_1_out, and_1_out);
  and and_3 (signal_2, OR_R1_FLAG, Opperation);
  D_Flip_Flop u_Init (.D(or_1_out), .clk(clk), .Q(Init), .preset(start));  // open: Qn, reset
  D_Flip_Flop u_Opperation (.D(or_2_out), .clk(clk), .Q(Opperation), .reset(undriven));  // open: Qn, preset
  or or_2 (or_2_out, signal_1, signal_2);
  Shifter #(.width(64)) shifter_2 (.in({R2_q_2, R2_q}), .\dist (6'b000001), .out(shifter_2_out));
  CsaveA CSA (
    .a(multiplexer_4_out), .b(multiplexer_1_out), .c(Result[31:0]), .s(CSA_s), .COUT2(CSA_cout2),
    .COUT1(CSA_cout1));  // open: cin, COUT0
  CsaveA CSA2 (
    .cin(or_3_out), .a(multiplexer_2_out), .b(multiplexer_3_out), .c(Result[63:32]), .s(CSA2_s));  // open: COUT2, COUT1, COUT0
  Shifter #(.shift("lr"), .width(32)) shifter_3 (.in(shifter_1_out), .\dist (5'b00001), .out(shifter_3_out));
  Shifter #(.width(64)) shifter_4 (.in(shifter_2_out), .\dist (6'b000001), .out(shifter_4_out));
  or or_3 (or_3_out, CSA_cout2, CSA_cout1);
  Multiplexer #(.width(32)) multiplexer_5 (.in0(CSA2_s), .in1(adder_1_out), .out(multiplexer_5_out), .sel(CSA_cout2));
  Adder #(.width(32)) adder_1 (.a(CSA2_s), .b(32'h1), .out(adder_1_out));  // open: cin, cout
  and and_4 (RE_signal, Opperation, not_2_out);
  not not_2 (not_2_out, OR_R1_FLAG);
  Multiplexer #(.width(32)) multiplexer_6 (.in0(shifter_3_out), .in1(a), .out(multiplexer_6_out), .sel(signal_1));
  or or_4 (or_4_out, signal_1, signal_2);
  Multiplexer #(.width(64)) multiplexer_7 (
    .in0({{32{1'b0}}, b}), .in1(shifter_4_out), .out(multiplexer_7_out), .sel(signal_2));
  or or_5 (or_5_out, RE_signal, signal_1);
  Multiplexer #(.width(64)) multiplexer_8 (
    .in0({64{1'b0}}), .in1({multiplexer_5_out, CSA_s}), .out(multiplexer_8_out), .sel(signal_2));
  Register #(.width(32)) R1 (.D(multiplexer_6_out), .en(or_4_out), .clk(clk), .Q(R1_q));  // open: clr
  Register #(.width(64)) R2 (.D(multiplexer_7_out), .en(or_4_out), .clk(clk), .Q({R2_q_2, R2_q}));  // open: clr
  Register #(.width(64)) R3 (.D(multiplexer_8_out), .en(or_4_out), .clk(clk), .Q(Result));  // open: clr
  Register #(.width(1)) RE (.D(RE_signal), .en(or_5_out), .clk(clk), .Q(RE_q));  // open: clr
  not not_3 (not_3_out, done);
  or or_6 (done, RE_q, RE_signal);
  Comparator #(.width(32)) comparator_1 (
    .a(R1_q), .b({32{1'b0}}), .gt(comparator_1_gt), .lt(comparator_1_lt));  // open: eq
  or or_7 (OR_R1_FLAG, comparator_1_gt, comparator_1_lt);

  // Other names for the same wires on the sheet: IN2[31:0] = b; IN1[31:0] = a; S = start
endmodule

module LSR (
  input  [31:0] a,
  input  [31:0] b,
  output [63:0] shifted
);

  wire comparator_1_eq, not_1_out;
  wire [31:0] multiplexer_1_out, subtractor_1_out;
  wire [63:0] multiplexer_2_out, shifter_1_out, shifter_2_out;

  Subtractor #(.width(32)) subtractor_1 (.a(b), .b(32'h1), .out(subtractor_1_out));  // open: bin, bout
  Multiplexer #(.width(32)) multiplexer_1 (.in0(subtractor_1_out), .in1(b), .out(multiplexer_1_out), .sel(b[0]));
  Comparator #(.width(5)) comparator_1 (.a(b[4:0]), .b({5{1'b0}}), .eq(comparator_1_eq));  // open: gt, lt
  Shifter #(.shift("lr"), .width(64)) shifter_1 (
    .in({{32{1'b0}}, a}), .\dist ({1'b0, multiplexer_1_out[4:0]}), .out(shifter_1_out));
  not not_1 (not_1_out, b[0]);
  Shifter #(.shift("lr"), .width(64)) shifter_2 (.in(shifter_1_out), .\dist (6'b000001), .out(shifter_2_out));
  Multiplexer #(.width(64)) multiplexer_2 (
    .in0(shifter_1_out), .in1(shifter_2_out), .out(multiplexer_2_out), .sel(not_1_out));
  Multiplexer #(.width(64)) multiplexer_3 (
    .in0(multiplexer_2_out), .in1({{32{1'b0}}, a}), .out(shifted), .sel(comparator_1_eq));
endmodule

module LSL (
  input  [31:0] a,
  input  [31:0] b,
  output [63:0] shifted
);

  wire comparator_1_eq, not_1_out;
  wire [31:0] multiplexer_1_out, subtractor_1_out;
  wire [63:0] multiplexer_2_out, shifter_1_out, shifter_2_out;

  Subtractor #(.width(32)) subtractor_1 (.a(b), .b(32'h1), .out(subtractor_1_out));  // open: bin, bout
  Multiplexer #(.width(32)) multiplexer_1 (.in0(subtractor_1_out), .in1(b), .out(multiplexer_1_out), .sel(b[0]));
  Comparator #(.width(5)) comparator_1 (.a(b[4:0]), .b({5{1'b0}}), .eq(comparator_1_eq));  // open: gt, lt
  Shifter #(.width(64)) shifter_1 (.in({{32{1'b0}}, a}), .\dist ({1'b0, multiplexer_1_out[4:0]}), .out(shifter_1_out));
  not not_1 (not_1_out, b[0]);
  Shifter #(.width(64)) shifter_2 (.in(shifter_1_out), .\dist (6'b000001), .out(shifter_2_out));
  Multiplexer #(.width(64)) multiplexer_2 (
    .in0(shifter_1_out), .in1(shifter_2_out), .out(multiplexer_2_out), .sel(not_1_out));
  Multiplexer #(.width(64)) multiplexer_3 (
    .in0(multiplexer_2_out), .in1({{32{1'b0}}, a}), .out(shifted), .sel(comparator_1_eq));
endmodule

module ASR (
  input  [31:0] a,
  input  [31:0] b,
  output [63:0] shifted
);

  wire comparator_1_lt;
  wire [31:0] multiplexer_1_out, not_1_out;
  wire [63:0] LogicalSR_shifted, not_2_out;

  assign not_1_out = ~a;  // NOT_Gate not_1, 32 bits wide
  Comparator #(.width(32)) comparator_1 (.a(a), .b({32{1'b0}}), .lt(comparator_1_lt));  // open: gt, eq
  Multiplexer #(.width(32)) multiplexer_1 (.in0(a), .in1(not_1_out), .out(multiplexer_1_out), .sel(comparator_1_lt));
  LSR LogicalSR (.a(multiplexer_1_out), .b(b), .shifted(LogicalSR_shifted));
  Multiplexer #(.width(64)) multiplexer_2 (
    .in0(LogicalSR_shifted), .in1(not_2_out), .out(shifted), .sel(comparator_1_lt));
  assign not_2_out = ~LogicalSR_shifted;  // NOT_Gate not_2, 64 bits wide
endmodule

module ROT_R (
  input  [31:0] a,
  input  [31:0] b,
  output [63:0] rotated
);

  wire [31:0] subtractor_1_out;
  wire [63:0] Logical_Shift_Left_shifted, Logical_Shift_Right_shifted, or_1_out;

  Subtractor #(.width(32)) subtractor_1 (.a(32'h20), .b(b), .out(subtractor_1_out));  // open: bin, bout
  LSR Logical_Shift_Right (.a(a), .b(b), .shifted(Logical_Shift_Right_shifted));
  LSL Logical_Shift_Left (.a(a), .b(subtractor_1_out), .shifted(Logical_Shift_Left_shifted));
  assign or_1_out = Logical_Shift_Right_shifted | Logical_Shift_Left_shifted;  // OR_Gate or_1, 64 bits wide
  assign rotated = or_1_out & 64'hffffffff;  // AND_Gate and_1, 64 bits wide
endmodule

module CL_Z (
  input  [31:0] a,
  output [63:0] num_Of_0
);

  wire comparator_1_lt, comparator_2_lt, comparator_3_lt, comparator_4_lt, comparator_5_lt, comparator_6_lt,
       comparator_7_lt, comparator_8_lt, comparator_9_lt, comparator_10_lt, comparator_11_lt,
       comparator_12_lt, comparator_13_lt, comparator_14_lt, comparator_15_lt, comparator_16_lt,
       comparator_17_lt, comparator_18_lt, comparator_19_lt, comparator_20_lt, comparator_21_lt,
       comparator_22_lt, comparator_23_lt, comparator_24_lt, comparator_25_lt, comparator_26_lt,
       comparator_27_lt, comparator_28_lt, comparator_29_lt, comparator_30_lt, comparator_31_lt,
       comparator_32_lt;
  wire [31:0] adder_1_out, adder_2_out, adder_3_out, adder_4_out, adder_5_out, adder_6_out, adder_7_out,
       adder_8_out, adder_9_out, adder_10_out, adder_11_out, adder_12_out, adder_13_out, adder_14_out,
       adder_15_out, adder_16_out, adder_17_out, adder_18_out, adder_19_out, adder_20_out, adder_21_out,
       adder_22_out, adder_23_out, adder_24_out, adder_25_out, adder_26_out, adder_27_out, adder_28_out,
       adder_29_out, adder_30_out, adder_31_out, bit_extender_1_out, bit_extender_2_out, bit_extender_3_out,
       bit_extender_4_out, bit_extender_5_out, bit_extender_6_out, bit_extender_7_out, bit_extender_8_out,
       bit_extender_9_out, bit_extender_10_out, bit_extender_11_out, bit_extender_12_out,
       bit_extender_13_out, bit_extender_14_out, bit_extender_15_out, bit_extender_16_out,
       bit_extender_17_out, bit_extender_18_out, bit_extender_19_out, bit_extender_20_out,
       bit_extender_21_out, bit_extender_22_out, bit_extender_23_out, bit_extender_24_out,
       bit_extender_25_out, bit_extender_26_out, bit_extender_27_out, bit_extender_28_out,
       bit_extender_29_out, bit_extender_30_out, bit_extender_31_out, bit_extender_32_out;
  wire [63:0] t;

  Comparator #(.width(64)) comparator_1 (.a(t), .b(64'h1), .lt(comparator_1_lt));  // open: gt, eq
  Comparator #(.width(64)) comparator_2 (.a(t), .b(64'h2), .lt(comparator_2_lt));  // open: gt, eq
  Comparator #(.width(64)) comparator_3 (.a(t), .b(64'h4), .lt(comparator_3_lt));  // open: gt, eq
  Comparator #(.width(64)) comparator_4 (.a(t), .b(64'h8), .lt(comparator_4_lt));  // open: gt, eq
  Comparator #(.width(64)) comparator_5 (.a(t), .b(64'h10), .lt(comparator_5_lt));  // open: gt, eq
  Comparator #(.width(64)) comparator_6 (.a(t), .b(64'h20), .lt(comparator_6_lt));  // open: gt, eq
  Comparator #(.width(64)) comparator_7 (.a(t), .b(64'h40), .lt(comparator_7_lt));  // open: gt, eq
  Comparator #(.width(64)) comparator_8 (.a(t), .b(64'h80), .lt(comparator_8_lt));  // open: gt, eq
  Comparator #(.width(64)) comparator_9 (.a(t), .b(64'h100), .lt(comparator_9_lt));  // open: gt, eq
  Comparator #(.width(64)) comparator_10 (.a(t), .b(64'h200), .lt(comparator_10_lt));  // open: gt, eq
  Comparator #(.width(64)) comparator_11 (.a(t), .b(64'h400), .lt(comparator_11_lt));  // open: gt, eq
  Comparator #(.width(64)) comparator_12 (.a(t), .b(64'h800), .lt(comparator_12_lt));  // open: gt, eq
  Comparator #(.width(64)) comparator_13 (.a(t), .b(64'h1000), .lt(comparator_13_lt));  // open: gt, eq
  Comparator #(.width(64)) comparator_14 (.a(t), .b(64'h2000), .lt(comparator_14_lt));  // open: gt, eq
  Comparator #(.width(64)) comparator_15 (.a(t), .b(64'h4000), .lt(comparator_15_lt));  // open: gt, eq
  Comparator #(.width(64)) comparator_16 (.a(t), .b(64'h8000), .lt(comparator_16_lt));  // open: gt, eq
  Comparator #(.width(64)) comparator_17 (.a(t), .b(64'h10000), .lt(comparator_17_lt));  // open: gt, eq
  Comparator #(.width(64)) comparator_18 (.a(t), .b(64'h20000), .lt(comparator_18_lt));  // open: gt, eq
  Comparator #(.width(64)) comparator_19 (.a(t), .b(64'h40000), .lt(comparator_19_lt));  // open: gt, eq
  Comparator #(.width(64)) comparator_20 (.a(t), .b(64'h80000), .lt(comparator_20_lt));  // open: gt, eq
  Comparator #(.width(64)) comparator_21 (.a(t), .b(64'h100000), .lt(comparator_21_lt));  // open: gt, eq
  Comparator #(.width(64)) comparator_22 (.a(t), .b(64'h200000), .lt(comparator_22_lt));  // open: gt, eq
  Comparator #(.width(64)) comparator_23 (.a(t), .b(64'h400000), .lt(comparator_23_lt));  // open: gt, eq
  Comparator #(.width(64)) comparator_24 (.a(t), .b(64'h800000), .lt(comparator_24_lt));  // open: gt, eq
  Comparator #(.width(64)) comparator_25 (.a(t), .b(64'h1000000), .lt(comparator_25_lt));  // open: gt, eq
  Comparator #(.width(64)) comparator_26 (.a(t), .b(64'h2000000), .lt(comparator_26_lt));  // open: gt, eq
  Comparator #(.width(64)) comparator_27 (.a(t), .b(64'h4000000), .lt(comparator_27_lt));  // open: gt, eq
  Comparator #(.width(64)) comparator_28 (.a(t), .b(64'h8000000), .lt(comparator_28_lt));  // open: gt, eq
  Comparator #(.width(64)) comparator_29 (.a(t), .b(64'h10000000), .lt(comparator_29_lt));  // open: gt, eq
  Comparator #(.width(64)) comparator_30 (.a(t), .b(64'h20000000), .lt(comparator_30_lt));  // open: gt, eq
  Comparator #(.width(64)) comparator_31 (.a(t), .b(64'h40000000), .lt(comparator_31_lt));  // open: gt, eq
  Comparator #(.width(64)) comparator_32 (.a(t), .b(64'h80000000), .lt(comparator_32_lt));  // open: gt, eq
  assign bit_extender_1_out = {{31{1'b0}}, comparator_1_lt};  // Bit_Extender bit_extender_1
  assign bit_extender_2_out = {{31{1'b0}}, comparator_2_lt};  // Bit_Extender bit_extender_2
  assign bit_extender_3_out = {{31{1'b0}}, comparator_3_lt};  // Bit_Extender bit_extender_3
  assign bit_extender_4_out = {{31{1'b0}}, comparator_4_lt};  // Bit_Extender bit_extender_4
  assign bit_extender_5_out = {{31{1'b0}}, comparator_5_lt};  // Bit_Extender bit_extender_5
  assign bit_extender_6_out = {{31{1'b0}}, comparator_6_lt};  // Bit_Extender bit_extender_6
  assign bit_extender_7_out = {{31{1'b0}}, comparator_7_lt};  // Bit_Extender bit_extender_7
  assign bit_extender_8_out = {{31{1'b0}}, comparator_8_lt};  // Bit_Extender bit_extender_8
  assign bit_extender_9_out = {{31{1'b0}}, comparator_9_lt};  // Bit_Extender bit_extender_9
  assign bit_extender_10_out = {{31{1'b0}}, comparator_10_lt};  // Bit_Extender bit_extender_10
  assign bit_extender_11_out = {{31{1'b0}}, comparator_11_lt};  // Bit_Extender bit_extender_11
  assign bit_extender_12_out = {{31{1'b0}}, comparator_12_lt};  // Bit_Extender bit_extender_12
  assign bit_extender_13_out = {{31{1'b0}}, comparator_13_lt};  // Bit_Extender bit_extender_13
  assign bit_extender_14_out = {{31{1'b0}}, comparator_14_lt};  // Bit_Extender bit_extender_14
  assign bit_extender_15_out = {{31{1'b0}}, comparator_15_lt};  // Bit_Extender bit_extender_15
  assign bit_extender_16_out = {{31{1'b0}}, comparator_16_lt};  // Bit_Extender bit_extender_16
  assign bit_extender_17_out = {{31{1'b0}}, comparator_17_lt};  // Bit_Extender bit_extender_17
  assign bit_extender_18_out = {{31{1'b0}}, comparator_18_lt};  // Bit_Extender bit_extender_18
  assign bit_extender_19_out = {{31{1'b0}}, comparator_19_lt};  // Bit_Extender bit_extender_19
  assign bit_extender_20_out = {{31{1'b0}}, comparator_20_lt};  // Bit_Extender bit_extender_20
  assign bit_extender_21_out = {{31{1'b0}}, comparator_21_lt};  // Bit_Extender bit_extender_21
  assign bit_extender_22_out = {{31{1'b0}}, comparator_22_lt};  // Bit_Extender bit_extender_22
  assign bit_extender_23_out = {{31{1'b0}}, comparator_23_lt};  // Bit_Extender bit_extender_23
  assign bit_extender_24_out = {{31{1'b0}}, comparator_24_lt};  // Bit_Extender bit_extender_24
  assign bit_extender_25_out = {{31{1'b0}}, comparator_25_lt};  // Bit_Extender bit_extender_25
  assign bit_extender_26_out = {{31{1'b0}}, comparator_26_lt};  // Bit_Extender bit_extender_26
  assign bit_extender_27_out = {{31{1'b0}}, comparator_27_lt};  // Bit_Extender bit_extender_27
  assign bit_extender_28_out = {{31{1'b0}}, comparator_28_lt};  // Bit_Extender bit_extender_28
  assign bit_extender_29_out = {{31{1'b0}}, comparator_29_lt};  // Bit_Extender bit_extender_29
  assign bit_extender_30_out = {{31{1'b0}}, comparator_30_lt};  // Bit_Extender bit_extender_30
  assign bit_extender_31_out = {{31{1'b0}}, comparator_31_lt};  // Bit_Extender bit_extender_31
  assign bit_extender_32_out = {{31{1'b0}}, comparator_32_lt};  // Bit_Extender bit_extender_32
  Adder #(.width(32)) adder_1 (.a(bit_extender_1_out), .b(bit_extender_2_out), .out(adder_1_out));  // open: cin, cout
  Adder #(.width(32)) adder_2 (.a(adder_1_out), .b(bit_extender_3_out), .out(adder_2_out));  // open: cin, cout
  Adder #(.width(32)) adder_3 (.a(adder_2_out), .b(bit_extender_4_out), .out(adder_3_out));  // open: cin, cout
  Adder #(.width(32)) adder_4 (.a(adder_3_out), .b(bit_extender_5_out), .out(adder_4_out));  // open: cin, cout
  Adder #(.width(32)) adder_5 (.a(adder_4_out), .b(bit_extender_6_out), .out(adder_5_out));  // open: cin, cout
  Adder #(.width(32)) adder_6 (.a(adder_5_out), .b(bit_extender_7_out), .out(adder_6_out));  // open: cin, cout
  Adder #(.width(32)) adder_7 (.a(adder_6_out), .b(bit_extender_8_out), .out(adder_7_out));  // open: cin, cout
  Adder #(.width(32)) adder_8 (.a(adder_7_out), .b(bit_extender_9_out), .out(adder_8_out));  // open: cin, cout
  Adder #(.width(32)) adder_9 (.a(adder_8_out), .b(bit_extender_10_out), .out(adder_9_out));  // open: cin, cout
  Adder #(.width(32)) adder_10 (.a(adder_9_out), .b(bit_extender_11_out), .out(adder_10_out));  // open: cin, cout
  Adder #(.width(32)) adder_11 (.a(adder_10_out), .b(bit_extender_12_out), .out(adder_11_out));  // open: cin, cout
  Adder #(.width(32)) adder_12 (.a(adder_11_out), .b(bit_extender_13_out), .out(adder_12_out));  // open: cin, cout
  Adder #(.width(32)) adder_13 (.a(adder_12_out), .b(bit_extender_14_out), .out(adder_13_out));  // open: cin, cout
  Adder #(.width(32)) adder_14 (.a(adder_13_out), .b(bit_extender_15_out), .out(adder_14_out));  // open: cin, cout
  Adder #(.width(32)) adder_15 (.a(adder_14_out), .b(bit_extender_16_out), .out(adder_15_out));  // open: cin, cout
  Adder #(.width(32)) adder_16 (.a(adder_15_out), .b(bit_extender_17_out), .out(adder_16_out));  // open: cin, cout
  Adder #(.width(32)) adder_17 (.a(adder_16_out), .b(bit_extender_18_out), .out(adder_17_out));  // open: cin, cout
  Adder #(.width(32)) adder_18 (.a(adder_17_out), .b(bit_extender_19_out), .out(adder_18_out));  // open: cin, cout
  Adder #(.width(32)) adder_19 (.a(adder_18_out), .b(bit_extender_20_out), .out(adder_19_out));  // open: cin, cout
  Adder #(.width(32)) adder_20 (.a(adder_19_out), .b(bit_extender_21_out), .out(adder_20_out));  // open: cin, cout
  Adder #(.width(32)) adder_21 (.a(adder_20_out), .b(bit_extender_22_out), .out(adder_21_out));  // open: cin, cout
  Adder #(.width(32)) adder_22 (.a(adder_21_out), .b(bit_extender_23_out), .out(adder_22_out));  // open: cin, cout
  Adder #(.width(32)) adder_23 (.a(adder_22_out), .b(bit_extender_24_out), .out(adder_23_out));  // open: cin, cout
  Adder #(.width(32)) adder_24 (.a(adder_23_out), .b(bit_extender_25_out), .out(adder_24_out));  // open: cin, cout
  Adder #(.width(32)) adder_25 (.a(adder_24_out), .b(bit_extender_26_out), .out(adder_25_out));  // open: cin, cout
  Adder #(.width(32)) adder_26 (.a(adder_25_out), .b(bit_extender_27_out), .out(adder_26_out));  // open: cin, cout
  Adder #(.width(32)) adder_27 (.a(adder_26_out), .b(bit_extender_28_out), .out(adder_27_out));  // open: cin, cout
  Adder #(.width(32)) adder_28 (.a(adder_27_out), .b(bit_extender_29_out), .out(adder_28_out));  // open: cin, cout
  Adder #(.width(32)) adder_29 (.a(adder_28_out), .b(bit_extender_30_out), .out(adder_29_out));  // open: cin, cout
  Adder #(.width(32)) adder_30 (.a(adder_29_out), .b(bit_extender_31_out), .out(adder_30_out));  // open: cin, cout
  Adder #(.width(32)) adder_31 (.a(adder_30_out), .b(bit_extender_32_out), .out(adder_31_out));  // open: cin, cout
  assign num_Of_0 = {{32{1'b0}}, adder_31_out};  // Bit_Extender bit_extender_33
  assign t = {{32{1'b0}}, a};  // Bit_Extender bit_extender_34
endmodule

module CL_O (
  input  [31:0] in_1,
  output [63:0] num_Of_1
);

  wire [31:0] not_1_out;

  assign not_1_out = ~in_1;  // NOT_Gate not_1, 32 bits wide
  CL_Z cl_z_1 (.a(not_1_out), .num_Of_0(num_Of_1));
endmodule
